// Logisim project P0_L0_CRC.circ as structural Verilog: 2 circuits, main circuit CRC
module CRC (
  input  [7:0] A,
  input  [3:0] B,
  output [10:0] C
);

  wire [2:0] n4div2_1_c, n4div2_2_c, n4div2_3_c, n4div2_4_c, n4div2_5_c, n4div2_6_c;
  wire [3:1] n4div2_7_c;

  _4div2 u_4div2_1 (.A(A[7:4]), .B(B), .C(n4div2_1_c));  // open: D
  _4div2 u_4div2_2 (.A({n4div2_1_c, A[3]}), .B(B), .C(n4div2_2_c));  // open: D
  _4div2 u_4div2_3 (.A({n4div2_2_c, A[2]}), .B(B), .C(n4div2_3_c));  // open: D
  _4div2 u_4div2_4 (.A({n4div2_3_c, A[1]}), .B(B), .C(n4div2_4_c));  // open: D
  _4div2 u_4div2_5 (.A({n4div2_4_c, A[0]}), .B(B), .C(n4div2_5_c));  // open: D
  _4div2 u_4div2_6 (.A({n4div2_5_c, 1'b0}), .B(B), .C(n4div2_6_c));  // open: D
  _4div2 u_4div2_7 (.A({n4div2_6_c, 1'b0}), .B(B), .C(n4div2_7_c));  // open: D
  _4div2 u_4div2_8 (.A({n4div2_7_c, 1'b0}), .B(B), .C(C[2:0]));  // open: D

  assign C[10:3] = A;
endmodule

module _4div2 (
  input  [3:0] A,
  input  [3:0] B,
  output D,
  output [2:0] C
);

  wire [3:0] xor_1_out;

  assign xor_1_out = A ^ B;  // XOR_Gate xor_1, 4 bits wide
  Multiplexer #(.width(3)) multiplexer_1 (.in0(A[2:0]), .in1(xor_1_out[2:0]), .out(C), .sel(A[3]));  // open: en

  assign D = A[3];
endmodule
