// Logisim project P0_L0_FSM.circ as structural Verilog: 3 circuits, main circuit fsm
module fsm (
  input  [1:0] in,
  input  clr,
  output out
);

  wire clk_out, register_1_q;
  wire [1:0] next_status_1_next_status0, register_2_q;

  // Probe on next_status_1_next_status0
  next_status next_status_1 (
    .in_1(in[1]), .in_0(in[0]), .next_status1(next_status_1_next_status0[1]), .status_1(register_2_q[1]),
    .status_0(register_2_q[0]), .next_status0(next_status_1_next_status0[0]));
  Register #(.width(1)) register_1 (.D(clr), .Q(register_1_q), .clk(clk_out), .clr(register_1_q));  // open: en
  // Probe on register_2_q
  Register #(.width(2)) register_2 (
    .D(next_status_1_next_status0), .Q(register_2_q), .clk(clk_out), .clr(register_1_q));  // open: en
  Clock clk (.out(clk_out));
  \output  output_1 (.in_1(in[1]), .out(out), .in_0(in[0]), .status_1(register_2_q[1]), .status_0(register_2_q[0]));

  // Notes on the sheet:
  //   sync reset
endmodule

module next_status (
  input  in_1,
  input  in_0,
  input  status_1,
  input  status_0,
  output next_status1,
  output next_status0
);

  wire and_1_out, and_2_out, and_3_out, and_4_out, and_5_out, and_6_out, and_7_out, and_8_out, and_9_out,
       not_1_out, not_2_out, not_3_out, not_4_out, not_5_out, not_6_out, not_7_out, not_8_out, not_9_out,
       or_2_out;

  not not_1 (not_1_out, in_0);
  and and_1 (and_1_out, not_1_out, not_2_out);
  not not_2 (not_2_out, status_1);
  not not_3 (not_3_out, in_0);
  and and_2 (and_2_out, not_3_out, status_1);
  not not_4 (not_4_out, status_0);
  not not_5 (not_5_out, in_0);
  and and_3 (and_3_out, not_5_out, not_6_out);
  not not_6 (not_6_out, status_1);
  not not_7 (not_7_out, in_0);
  and and_4 (and_4_out, not_7_out, status_1);
  not not_8 (not_8_out, status_0);
  and and_5 (and_5_out, and_1_out, status_0);
  and and_6 (and_6_out, and_2_out, not_4_out);
  and and_7 (and_7_out, and_3_out, status_0);
  and and_8 (and_8_out, and_4_out, not_8_out);
  not not_9 (not_9_out, in_1);
  or or_1 (next_status1, and_5_out, and_6_out);
  or or_2 (or_2_out, and_7_out, and_8_out);
  and and_9 (and_9_out, not_9_out, in_0);
  or or_3 (next_status0, or_2_out, and_9_out);
endmodule

module \output  (
  input  in_1,
  input  in_0,
  input  status_1,
  input  status_0,
  output out
);

  wire and_1_out, not_1_out;

  not not_1 (not_1_out, in_0);
  and and_1 (and_1_out, not_1_out, status_1);
  and and_2 (out, and_1_out, status_0);
endmodule
