// Logisim project P0_L0_GRF.circ as structural Verilog: 1 circuit, main circuit grf
module grf (
  input  [31:0] WD,
  input  [4:0] A1,
  input  [4:0] A2,
  input  [4:0] A3,
  input  clk,
  input  reset,
  input  WE,
  output [31:0] RD1,
  output [31:0] RD2
);

  wire demultiplexer_1_out0, demultiplexer_1_out1, demultiplexer_1_out2, demultiplexer_1_out3, Write_00000,
       Write_00001, Write_00010, Write_00011, Write_00100, Write_00101, Write_00110, Write_00111,
       Write_01000, Write_01001, Write_01010, Write_01011, Write_01100, Write_01101, Write_01110,
       Write_01111, Write_10000, Write_10001, Write_10010, Write_10011, Write_10100, Write_10101,
       Write_10110, Write_10111, Write_11000, Write_11001, Write_11010, Write_11011, Write_11100,
       Write_11101, Write_11110, Write_11111;
  wire [31:0] multiplexer_1_out, multiplexer_2_out, multiplexer_3_out, multiplexer_4_out, multiplexer_6_out,
       multiplexer_7_out, multiplexer_8_out, multiplexer_9_out, Read_00000, Read_00001, Read_00010,
       Read_00011, Read_00100, Read_00101, Read_00110, Read_00111, Read_01000, Read_01001, Read_01010,
       Read_01011, Read_01100, Read_01101, Read_01110, Read_01111, Read_10000, Read_10001, Read_10010,
       Read_10011, Read_10100, Read_10101, Read_10110, Read_10111, Read_11000, Read_11001, Read_11010,
       Read_11011, Read_11100, Read_11101, Read_11110, Read_11111;

  Register #(.width(32)) register_1 (.D({32{1'b0}}), .en(Write_00000), .Q(Read_00000), .clk(clk), .clr(reset));
  Register #(.width(32)) register_2 (.D(WD), .en(Write_00001), .Q(Read_00001), .clk(clk), .clr(reset));
  Register #(.width(32)) register_3 (.D(WD), .en(Write_00010), .Q(Read_00010), .clk(clk), .clr(reset));
  Register #(.width(32)) register_4 (.D(WD), .en(Write_00011), .Q(Read_00011), .clk(clk), .clr(reset));
  Register #(.width(32)) register_5 (.D(WD), .en(Write_00100), .Q(Read_00100), .clk(clk), .clr(reset));
  Register #(.width(32)) register_6 (.D(WD), .en(Write_00101), .Q(Read_00101), .clk(clk), .clr(reset));
  Register #(.width(32)) register_7 (.D(WD), .en(Write_00110), .Q(Read_00110), .clk(clk), .clr(reset));
  Register #(.width(32)) register_8 (.D(WD), .en(Write_00111), .Q(Read_00111), .clk(clk), .clr(reset));
  Demultiplexer #(.select(2), .disabled(0)) demultiplexer_1 (
    .out0(demultiplexer_1_out0), .out1(demultiplexer_1_out1), .out2(demultiplexer_1_out2),
    .out3(demultiplexer_1_out3), .in(WE), .sel(A3[4:3]));  // open: en
  Demultiplexer #(.select(3)) demultiplexer_2 (
    .out0(Write_00000), .out1(Write_00001), .out2(Write_00010), .out3(Write_00011), .out4(Write_00100),
    .out5(Write_00101), .out6(Write_00110), .out7(Write_00111), .in(demultiplexer_1_out0), .sel(A3[2:0]));  // open: en
  Demultiplexer #(.select(3)) demultiplexer_3 (
    .out0(Write_01000), .out1(Write_01001), .out2(Write_01010), .out3(Write_01011), .out4(Write_01100),
    .out5(Write_01101), .out6(Write_01110), .out7(Write_01111), .in(demultiplexer_1_out1), .sel(A3[2:0]));  // open: en
  Demultiplexer #(.select(3)) demultiplexer_4 (
    .out0(Write_10000), .out1(Write_10001), .out2(Write_10010), .out3(Write_10011), .out4(Write_10100),
    .out5(Write_10101), .out6(Write_10110), .out7(Write_10111), .in(demultiplexer_1_out2), .sel(A3[2:0]));  // open: en
  Demultiplexer #(.select(3)) demultiplexer_5 (
    .out0(Write_11000), .out1(Write_11001), .out2(Write_11010), .out3(Write_11011), .out4(Write_11100),
    .out5(Write_11101), .out6(Write_11110), .out7(Write_11111), .in(demultiplexer_1_out3), .sel(A3[2:0]));  // open: en
  Multiplexer #(.select(3), .width(32)) multiplexer_1 (
    .in0(Read_00000), .in1(Read_00001), .in2(Read_00010), .in3(Read_00011), .in4(Read_00100),
    .in5(Read_00101), .in6(Read_00110), .in7(Read_00111), .out(multiplexer_1_out), .sel(A1[2:0]));  // open: en
  Multiplexer #(.select(3), .width(32)) multiplexer_2 (
    .in0(Read_01000), .in1(Read_01001), .in2(Read_01010), .in3(Read_01011), .in4(Read_01100),
    .in5(Read_01101), .in6(Read_01110), .in7(Read_01111), .out(multiplexer_2_out), .sel(A1[2:0]));  // open: en
  Multiplexer #(.select(3), .width(32)) multiplexer_3 (
    .in0(Read_10000), .in1(Read_10001), .in2(Read_10010), .in3(Read_10011), .in4(Read_10100),
    .in5(Read_10101), .in6(Read_10110), .in7(Read_10111), .out(multiplexer_3_out), .sel(A1[2:0]));  // open: en
  Multiplexer #(.select(3), .width(32)) multiplexer_4 (
    .in0(Read_11000), .in1(Read_11001), .in2(Read_11010), .in3(Read_11011), .in4(Read_11100),
    .in5(Read_11101), .in6(Read_11110), .in7(Read_11111), .out(multiplexer_4_out), .sel(A1[2:0]));  // open: en
  Register #(.width(32)) register_9 (.D(WD), .en(Write_01000), .Q(Read_01000), .clk(clk), .clr(reset));
  Register #(.width(32)) register_10 (.D(WD), .en(Write_01001), .Q(Read_01001), .clk(clk), .clr(reset));
  Register #(.width(32)) register_11 (.D(WD), .en(Write_01010), .Q(Read_01010), .clk(clk), .clr(reset));
  Register #(.width(32)) register_12 (.D(WD), .en(Write_01011), .Q(Read_01011), .clk(clk), .clr(reset));
  Register #(.width(32)) register_13 (.D(WD), .en(Write_01100), .Q(Read_01100), .clk(clk), .clr(reset));
  Register #(.width(32)) register_14 (.D(WD), .en(Write_01101), .Q(Read_01101), .clk(clk), .clr(reset));
  Register #(.width(32)) register_15 (.D(WD), .en(Write_01110), .Q(Read_01110), .clk(clk), .clr(reset));
  Register #(.width(32)) register_16 (.D(WD), .en(Write_01111), .Q(Read_01111), .clk(clk), .clr(reset));
  Multiplexer #(.select(2), .width(32)) multiplexer_5 (
    .in0(multiplexer_1_out), .in1(multiplexer_2_out), .in2(multiplexer_3_out), .in3(multiplexer_4_out),
    .out(RD1), .sel(A1[4:3]));  // open: en
  Register #(.width(32)) register_17 (.D(WD), .en(Write_10000), .Q(Read_10000), .clk(clk), .clr(reset));
  Register #(.width(32)) register_18 (.D(WD), .en(Write_10001), .Q(Read_10001), .clk(clk), .clr(reset));
  Register #(.width(32)) register_19 (.D(WD), .en(Write_10010), .Q(Read_10010), .clk(clk), .clr(reset));
  Register #(.width(32)) register_20 (.D(WD), .en(Write_10011), .Q(Read_10011), .clk(clk), .clr(reset));
  Register #(.width(32)) register_21 (.D(WD), .en(Write_10100), .Q(Read_10100), .clk(clk), .clr(reset));
  Register #(.width(32)) register_22 (.D(WD), .en(Write_10101), .Q(Read_10101), .clk(clk), .clr(reset));
  Register #(.width(32)) register_23 (.D(WD), .en(Write_10110), .Q(Read_10110), .clk(clk), .clr(reset));
  Register #(.width(32)) register_24 (.D(WD), .en(Write_10111), .Q(Read_10111), .clk(clk), .clr(reset));
  Multiplexer #(.select(3), .width(32)) multiplexer_6 (
    .in0(Read_00000), .in1(Read_00001), .in2(Read_00010), .in3(Read_00011), .in4(Read_00100),
    .in5(Read_00101), .in6(Read_00110), .in7(Read_00111), .out(multiplexer_6_out), .sel(A2[2:0]));  // open: en
  Multiplexer #(.select(3), .width(32)) multiplexer_7 (
    .in0(Read_01000), .in1(Read_01001), .in2(Read_01010), .in3(Read_01011), .in4(Read_01100),
    .in5(Read_01101), .in6(Read_01110), .in7(Read_01111), .out(multiplexer_7_out), .sel(A2[2:0]));  // open: en
  Multiplexer #(.select(3), .width(32)) multiplexer_8 (
    .in0(Read_10000), .in1(Read_10001), .in2(Read_10010), .in3(Read_10011), .in4(Read_10100),
    .in5(Read_10101), .in6(Read_10110), .in7(Read_10111), .out(multiplexer_8_out), .sel(A2[2:0]));  // open: en
  Multiplexer #(.select(3), .width(32)) multiplexer_9 (
    .in0(Read_11000), .in1(Read_11001), .in2(Read_11010), .in3(Read_11011), .in4(Read_11100),
    .in5(Read_11101), .in6(Read_11110), .in7(Read_11111), .out(multiplexer_9_out), .sel(A2[2:0]));  // open: en
  Register #(.width(32)) register_25 (.D(WD), .en(Write_11000), .Q(Read_11000), .clk(clk), .clr(reset));
  Register #(.width(32)) register_26 (.D(WD), .en(Write_11001), .Q(Read_11001), .clk(clk), .clr(reset));
  Register #(.width(32)) register_27 (.D(WD), .en(Write_11010), .Q(Read_11010), .clk(clk), .clr(reset));
  Register #(.width(32)) register_28 (.D(WD), .en(Write_11011), .Q(Read_11011), .clk(clk), .clr(reset));
  Register #(.width(32)) register_29 (.D(WD), .en(Write_11100), .Q(Read_11100), .clk(clk), .clr(reset));
  Register #(.width(32)) register_30 (.D(WD), .en(Write_11101), .Q(Read_11101), .clk(clk), .clr(reset));
  Register #(.width(32)) register_31 (.D(WD), .en(Write_11110), .Q(Read_11110), .clk(clk), .clr(reset));
  Register #(.width(32)) register_32 (.D(WD), .en(Write_11111), .Q(Read_11111), .clk(clk), .clr(reset));
  Multiplexer #(.select(2), .width(32)) multiplexer_10 (
    .in0(multiplexer_6_out), .in1(multiplexer_7_out), .in2(multiplexer_8_out), .in3(multiplexer_9_out),
    .out(RD2), .sel(A2[4:3]));  // open: en
endmodule
