// Logisim project P0_L1_ftoi.circ as structural Verilog: 2 circuits, main circuit ftoi
module ftoi (
  input  [15:0] float,
  output [31:0] \int 
);

  wire comparator_1_eq, comparator_2_eq;
  wire [4:0] subtractor_1_out;
  wire [31:0] adder_1_out, multiplexer_1_out, multiplexer_2_out, not_1_out, shifter_1_out_4;

  Comparator #(.width(5), .mode("unsigned")) comparator_1 (
    .a({5{1'b1}}), .b(float[14:10]), .eq(comparator_1_eq));  // open: gt, lt
  Comparator #(.width(5), .mode("unsigned")) comparator_2 (
    .a({5{1'b0}}), .b(float[14:10]), .eq(comparator_2_eq));  // open: gt, lt
  Subtractor #(.width(5)) subtractor_1 (.a(float[14:10]), .b(5'b01111), .out(subtractor_1_out));  // open: bin, bout
  Multiplexer #(.width(32)) multiplexer_1 (
    .in0(32'h1), .in1({32{1'b0}}), .out(multiplexer_1_out), .sel(comparator_2_eq));  // open: en
  shifter shifter_1 (
    .shiftbit(subtractor_1_out), .source(float[9:0]), .ans(multiplexer_1_out), .out_4(shifter_1_out_4));
  assign not_1_out = ~shifter_1_out_4;  // NOT_Gate not_1, 32 bits wide
  Adder #(.width(32)) adder_1 (.a(not_1_out), .b(32'h1), .out(adder_1_out));  // open: cin, cout
  Multiplexer #(.width(32)) multiplexer_2 (
    .in0(shifter_1_out_4), .in1(adder_1_out), .out(multiplexer_2_out), .sel(float[15]));  // open: en
  Multiplexer #(.width(32)) multiplexer_3 (
    .in0(multiplexer_2_out), .in1({32{1'b0}}), .out(\int ), .sel(comparator_1_eq));  // open: en

  // Notes on the sheet:
  //   exponent
  //   sign
  //   fraction
endmodule

module shifter (
  input  [4:0] shiftbit,
  input  [9:0] source,
  input  [31:0] ans,
  output [31:0] out_4
);

  wire [9:0] multiplexer_1_out, multiplexer_3_out, multiplexer_5_out, shifter_1_out, shifter_2_out,
       shifter_3_out, shifter_4_out;
  wire [31:0] multiplexer_2_out, multiplexer_4_out, multiplexer_6_out, multiplexer_8_out, shifter_5_out;

  Shifter #(.width(10)) shifter_1 (.in(source), .\dist (4'b0001), .out(shifter_1_out));
  Multiplexer #(.width(10)) multiplexer_1 (
    .in0(source), .in1(shifter_1_out), .out(multiplexer_1_out), .sel(shiftbit[0]));  // open: en
  Multiplexer #(.width(32)) multiplexer_2 (
    .in0(ans), .in1({ans[30:0], source[9]}), .out(multiplexer_2_out), .sel(shiftbit[0]));  // open: en
  Shifter #(.width(10)) shifter_2 (.in(multiplexer_1_out), .\dist (4'b0010), .out(shifter_2_out));
  Multiplexer #(.width(10)) multiplexer_3 (
    .in0(multiplexer_1_out), .in1(shifter_2_out), .out(multiplexer_3_out), .sel(shiftbit[1]));  // open: en
  Multiplexer #(.width(32)) multiplexer_4 (
    .in0(multiplexer_2_out), .in1({multiplexer_2_out[29:0], multiplexer_1_out[9:8]}),
    .out(multiplexer_4_out), .sel(shiftbit[1]));  // open: en
  Shifter #(.width(10)) shifter_3 (.in(multiplexer_3_out), .\dist (4'b0100), .out(shifter_3_out));
  Multiplexer #(.width(10)) multiplexer_5 (
    .in0(multiplexer_3_out), .in1(shifter_3_out), .out(multiplexer_5_out), .sel(shiftbit[2]));  // open: en
  Multiplexer #(.width(32)) multiplexer_6 (
    .in0(multiplexer_4_out), .in1({multiplexer_4_out[27:0], multiplexer_3_out[9:6]}),
    .out(multiplexer_6_out), .sel(shiftbit[2]));  // open: en
  Shifter #(.width(10)) shifter_4 (.in(multiplexer_5_out), .\dist (4'b1000), .out(shifter_4_out));
  Multiplexer #(.width(10)) multiplexer_7 (
    .in0(multiplexer_5_out), .in1(shifter_4_out), .sel(shiftbit[3]));  // open: out, en
  Multiplexer #(.width(32)) multiplexer_8 (
    .in0(multiplexer_6_out), .in1({multiplexer_6_out[23:0], multiplexer_5_out[9:2]}),
    .out(multiplexer_8_out), .sel(shiftbit[3]));  // open: en
  Shifter #(.width(32), .shift("lr")) shifter_5 (.in(multiplexer_8_out), .\dist (5'b10000), .out(shifter_5_out));
  Multiplexer #(.width(32)) multiplexer_9 (
    .in0(multiplexer_8_out), .in1(shifter_5_out), .out(out_4), .sel(shiftbit[4]));  // open: en
endmodule
