// Logisim project P0_L1_navigation_2020.circ as structural Verilog: 3 circuits, main circuit navigation
module navigation (
  input  [1:0] dir,
  input  clk,
  input  reset,
  output hit,
  output arrive
);

  wire [3:0] next_status_1_next_status_0, register_1_q;

  next_status next_status_1 (
    .status_3(register_1_q[3]), .status_2(register_1_q[2]), .status_1(register_1_q[1]),
    .status_0(register_1_q[0]), .dir_1(dir[1]), .dir_0(dir[0]),
    .next_status_3(next_status_1_next_status_0[3]), .next_status_2(next_status_1_next_status_0[2]),
    .next_status_1(next_status_1_next_status_0[1]), .next_status_0(next_status_1_next_status_0[0]));
  Register #(.width(4)) register_1 (
    .D(next_status_1_next_status_0), .Q(register_1_q), .clk(clk), .clr(reset));  // open: en
  \output  output_1 (
    .status_3(register_1_q[3]), .status_2(register_1_q[2]), .status_1(register_1_q[1]),
    .status_0(register_1_q[0]), .hit(hit), .arrive(arrive));
endmodule

module next_status (
  input  status_3,
  input  status_2,
  input  status_1,
  input  status_0,
  input  dir_1,
  input  dir_0,
  output next_status_3,
  output next_status_2,
  output next_status_1,
  output next_status_0
);

  wire and_1_out, and_2_out, and_3_out, and_4_out, and_5_out, and_6_out, and_7_out, and_8_out, and_9_out,
       and_10_out, and_11_out, and_12_out, and_13_out, and_14_out, and_15_out, and_16_out, and_17_out,
       and_18_out, and_19_out, and_20_out, and_21_out, and_22_out, and_23_out, and_24_out, and_25_out,
       and_26_out, and_27_out, and_28_out, and_29_out, and_30_out, and_31_out, and_32_out, and_33_out,
       and_34_out, and_35_out, and_36_out, and_37_out, and_38_out, and_39_out, and_40_out, and_41_out,
       and_42_out, and_43_out, not_1_out, not_2_out, not_3_out, not_4_out, not_5_out, not_6_out, not_7_out,
       not_8_out, not_9_out, not_10_out, not_11_out, not_12_out, not_13_out, not_14_out, not_15_out,
       not_16_out, not_17_out, not_18_out, not_19_out, not_20_out, not_21_out, not_22_out, not_23_out,
       not_24_out, not_25_out, not_26_out, not_27_out, not_28_out, or_1_out, or_2_out, or_4_out, or_5_out,
       or_6_out, or_7_out, or_9_out, or_10_out, or_12_out;

  not not_1 (not_1_out, status_2);
  not not_2 (not_2_out, status_0);
  not not_3 (not_3_out, dir_1);
  not not_4 (not_4_out, status_2);
  not not_5 (not_5_out, status_1);
  not not_6 (not_6_out, status_0);
  not not_7 (not_7_out, dir_1);
  not not_8 (not_8_out, dir_0);
  not not_9 (not_9_out, status_0);
  not not_10 (not_10_out, dir_1);
  not not_11 (not_11_out, dir_0);
  not not_12 (not_12_out, dir_1);
  not not_13 (not_13_out, status_1);
  not not_14 (not_14_out, dir_1);
  not not_15 (not_15_out, status_2);
  not not_16 (not_16_out, status_1);
  not not_17 (not_17_out, dir_1);
  not not_18 (not_18_out, dir_0);
  and and_1 (and_1_out, not_1_out, not_2_out);
  and and_2 (and_2_out, not_3_out, dir_0);
  and and_3 (and_3_out, not_4_out, not_5_out);
  and and_4 (and_4_out, not_6_out, dir_1);
  not not_19 (not_19_out, status_2);
  not not_20 (not_20_out, status_0);
  not not_21 (not_21_out, dir_0);
  and and_5 (and_5_out, status_0, dir_1);
  and and_6 (and_6_out, status_1, status_0);
  and and_7 (and_7_out, not_7_out, not_8_out);
  and and_8 (and_8_out, status_1, not_9_out);
  and and_9 (and_9_out, not_10_out, not_11_out);
  and and_10 (and_10_out, status_1, status_0);
  and and_11 (and_11_out, not_12_out, dir_0);
  and and_12 (and_12_out, not_13_out, status_0);
  not not_22 (not_22_out, dir_1);
  and and_13 (and_13_out, status_0, not_14_out);
  not not_23 (not_23_out, dir_0);
  not not_24 (not_24_out, status_0);
  not not_25 (not_25_out, dir_1);
  not not_26 (not_26_out, status_0);
  not not_27 (not_27_out, dir_0);
  and and_14 (and_14_out, not_15_out, not_16_out);
  and and_15 (and_15_out, not_17_out, not_18_out);
  and and_16 (and_16_out, status_0, dir_1);
  and and_17 (and_17_out, status_1, dir_1);
  and and_18 (and_18_out, status_1, status_0);
  not not_28 (not_28_out, dir_0);
  and and_19 (and_19_out, and_1_out, and_2_out);
  and and_20 (and_20_out, and_3_out, and_4_out);
  and and_21 (and_21_out, not_19_out, not_20_out);
  and and_22 (and_22_out, dir_1, not_21_out);
  and and_23 (and_23_out, and_5_out, dir_0);
  and and_24 (and_24_out, and_6_out, and_7_out);
  and and_25 (and_25_out, and_8_out, and_9_out);
  and and_26 (and_26_out, and_10_out, and_11_out);
  and and_27 (and_27_out, and_12_out, not_22_out);
  and and_28 (and_28_out, and_13_out, not_23_out);
  and and_29 (and_29_out, status_1, not_24_out);
  and and_30 (and_30_out, not_25_out, dir_0);
  and and_31 (and_31_out, status_1, not_26_out);
  and and_32 (and_32_out, dir_1, not_27_out);
  and and_33 (and_33_out, status_1, status_0);
  and and_34 (and_34_out, dir_1, dir_0);
  and and_35 (and_35_out, and_14_out, and_15_out);
  and and_36 (and_36_out, and_16_out, dir_0);
  and and_37 (and_37_out, and_17_out, dir_0);
  and and_38 (and_38_out, and_18_out, not_28_out);
  or or_1 (or_1_out, and_19_out, and_20_out);
  and and_39 (and_39_out, and_21_out, and_22_out);
  or or_2 (or_2_out, and_23_out, and_24_out);
  and and_40 (and_40_out, status_3, status_2);
  or or_3 (next_status_2, and_25_out, and_26_out);
  or or_4 (or_4_out, and_27_out, and_28_out);
  and and_41 (and_41_out, and_29_out, and_30_out);
  and and_42 (and_42_out, and_31_out, and_32_out);
  and and_43 (and_43_out, and_33_out, and_34_out);
  or or_5 (or_5_out, and_35_out, and_36_out);
  or or_6 (or_6_out, and_37_out, and_38_out);
  or or_7 (or_7_out, or_1_out, and_39_out);
  or or_8 (next_status_3, or_7_out, or_9_out);
  or or_9 (or_9_out, or_2_out, and_40_out);
  or or_10 (or_10_out, or_4_out, and_41_out);
  or or_11 (next_status_1, or_10_out, or_12_out);
  or or_12 (or_12_out, and_42_out, and_43_out);
  or or_13 (next_status_0, or_5_out, or_6_out);
endmodule

module \output  (
  input  status_3,
  input  status_2,
  input  status_1,
  input  status_0,
  output hit,
  output arrive
);

  wire and_1_out, and_2_out, not_1_out, not_2_out, not_3_out;

  not not_1 (not_1_out, status_3);
  and and_1 (and_1_out, not_1_out, status_2);
  not not_2 (not_2_out, status_1);
  and and_2 (and_2_out, not_2_out, not_3_out);
  not not_3 (not_3_out, status_0);
  and and_3 (arrive, and_1_out, and_2_out);

  assign hit = status_3;
endmodule
