// Logisim project P3_L0_CPU - more_instr.circ as structural Verilog: 8 circuits, main circuit main
module main (
  input  reset,
  output halt,
  output [31:0] Instr,
  output RegWrite,
  output [4:0] RegAddr,
  output [31:0] RegData,
  output MemWrite,
  output [4:0] MemAddr,
  output [31:0] MemData
);

  wire ALUASel, ALUBSel, clk_out, comparator_1_eq, comparator_1_lt, EXTOp, LessZero, Zero;
  wire [1:0] DMOp, WDSel, WRA3Sel;
  wire [2:0] ALUOp, NPCOp;
  wire [31:0] alu_1_c, dm_1_rd, ext_1_output, multiplexer_3_out, multiplexer_4_out, npc_1_npc, npc_1_pc_4,
       PC_q, rs;

  or or_1 (halt, comparator_1_eq, comparator_1_lt);
  Comparator #(.width(32), .mode("unsigned")) comparator_1 (
    .a(32'h22), .b(PC_q), .eq(comparator_1_eq), .lt(comparator_1_lt));  // open: gt
  NPC npc_1 (
    .PC(PC_q), .Zero(Zero), .Imm(Instr[25:0]), .LessZero(LessZero), .NPCOp(NPCOp), .rs(rs),
    .PC_4(npc_1_pc_4), .NPC(npc_1_npc));
  Clock clk (.out(clk_out));
  Register #(.width(32)) PC (.D(npc_1_npc), .Q(PC_q), .clk(clk_out), .clr(reset));  // open: en
  IM im_1 (.PC(PC_q), .Instr(Instr));
  Multiplexer #(.select(2), .width(5)) multiplexer_1 (
    .in0(Instr[15:11]), .in1(Instr[20:16]), .in2({5{1'b1}}), .out(RegAddr), .sel(WRA3Sel));  // open: in3, en
  CTRL ctrl_1 (
    .ALUOp(ALUOp), .DMOp(DMOp), .NPCOp(NPCOp), .WRA3Sel(WRA3Sel), .WDSel(WDSel), .EXTOp(EXTOp),
    .WE(RegWrite), .ALUBSel(ALUBSel), .DMWr(MemWrite), .opcode(Instr[31:26]), .funct(Instr[5:0]),
    .ALUASel(ALUASel));
  Multiplexer #(.select(2), .width(32)) multiplexer_2 (
    .in0(dm_1_rd), .in1({alu_1_c[31:7], MemAddr, alu_1_c[1:0]}), .in2(npc_1_pc_4), .out(RegData), .sel(WDSel));  // open: in3, en
  EXT ext_1 (.EXTOp(EXTOp), .Imm(Instr[15:0]), .Output(ext_1_output));
  GRF grf_1 (
    .WD(RegData), .A1(Instr[25:21]), .A2(Instr[20:16]), .A3(RegAddr), .clk(clk_out), .reset(reset),
    .WE(RegWrite), .RD1(rs), .RD2(MemData));
  Multiplexer #(.width(32)) multiplexer_3 (.in0(rs), .in1(Instr), .out(multiplexer_3_out), .sel(ALUASel));  // open: en
  Multiplexer #(.width(32)) multiplexer_4 (
    .in0(MemData), .in1(ext_1_output), .out(multiplexer_4_out), .sel(ALUBSel));  // open: en
  ALU alu_1 (
    .ALUOp(ALUOp), .Zero(Zero), .LessZero(LessZero), .C({alu_1_c[31:7], MemAddr, alu_1_c[1:0]}),
    .A(multiplexer_3_out), .B(multiplexer_4_out));
  DM dm_1 (
    .Addr({alu_1_c[31:7], MemAddr, alu_1_c[1:0]}), .WD(MemData), .DMOp(DMOp), .RD(dm_1_rd),
    .DMWrite(MemWrite), .clk(clk_out), .reset(reset));

  // Other names for the same wires on the sheet: DMWr = MemWrite; WE = RegWrite

  // Notes on the sheet:
  //   opcode
  //   funct
  //   NPCImm
endmodule

module GRF (
  input  [31:0] WD,
  input  [4:0] A1,
  input  [4:0] A2,
  input  [4:0] A3,
  input  clk,
  input  reset,
  input  WE,
  output [31:0] RD1,
  output [31:0] RD2
);

  wire demultiplexer_1_out0, demultiplexer_1_out1, demultiplexer_1_out2, demultiplexer_1_out3, Write_00000,
       Write_00001, Write_00010, Write_00011, Write_00100, Write_00101, Write_00110, Write_00111,
       Write_01000, Write_01001, Write_01010, Write_01011, Write_01100, Write_01101, Write_01110,
       Write_01111, Write_10000, Write_10001, Write_10010, Write_10011, Write_10100, Write_10101,
       Write_10110, Write_10111, Write_11000, Write_11001, Write_11010, Write_11011, Write_11100,
       Write_11101, Write_11110, Write_11111;
  wire [31:0] multiplexer_1_out, multiplexer_2_out, multiplexer_3_out, multiplexer_4_out, multiplexer_6_out,
       multiplexer_7_out, multiplexer_8_out, multiplexer_9_out, Read_00000, Read_00001, Read_00010,
       Read_00011, Read_00100, Read_00101, Read_00110, Read_00111, Read_01000, Read_01001, Read_01010,
       Read_01011, Read_01100, Read_01101, Read_01110, Read_01111, Read_10000, Read_10001, Read_10010,
       Read_10011, Read_10100, Read_10101, Read_10110, Read_10111, Read_11000, Read_11001, Read_11010,
       Read_11011, Read_11100, Read_11101, Read_11110, Read_11111;

  Register #(.width(32)) register_1 (.D({32{1'b0}}), .en(Write_00000), .Q(Read_00000), .clk(clk), .clr(reset));
  Register #(.width(32)) register_2 (.D(WD), .en(Write_00001), .Q(Read_00001), .clk(clk), .clr(reset));
  Register #(.width(32)) register_3 (.D(WD), .en(Write_00010), .Q(Read_00010), .clk(clk), .clr(reset));
  Register #(.width(32)) register_4 (.D(WD), .en(Write_00011), .Q(Read_00011), .clk(clk), .clr(reset));
  Register #(.width(32)) register_5 (.D(WD), .en(Write_00100), .Q(Read_00100), .clk(clk), .clr(reset));
  Register #(.width(32)) register_6 (.D(WD), .en(Write_00101), .Q(Read_00101), .clk(clk), .clr(reset));
  Register #(.width(32)) register_7 (.D(WD), .en(Write_00110), .Q(Read_00110), .clk(clk), .clr(reset));
  Register #(.width(32)) register_8 (.D(WD), .en(Write_00111), .Q(Read_00111), .clk(clk), .clr(reset));
  Demultiplexer #(.select(2), .disabled(0)) demultiplexer_1 (
    .out0(demultiplexer_1_out0), .out1(demultiplexer_1_out1), .out2(demultiplexer_1_out2),
    .out3(demultiplexer_1_out3), .in(WE), .sel(A3[4:3]));  // open: en
  Demultiplexer #(.select(3)) demultiplexer_2 (
    .out0(Write_00000), .out1(Write_00001), .out2(Write_00010), .out3(Write_00011), .out4(Write_00100),
    .out5(Write_00101), .out6(Write_00110), .out7(Write_00111), .in(demultiplexer_1_out0), .sel(A3[2:0]));  // open: en
  Demultiplexer #(.select(3)) demultiplexer_3 (
    .out0(Write_01000), .out1(Write_01001), .out2(Write_01010), .out3(Write_01011), .out4(Write_01100),
    .out5(Write_01101), .out6(Write_01110), .out7(Write_01111), .in(demultiplexer_1_out1), .sel(A3[2:0]));  // open: en
  Demultiplexer #(.select(3)) demultiplexer_4 (
    .out0(Write_10000), .out1(Write_10001), .out2(Write_10010), .out3(Write_10011), .out4(Write_10100),
    .out5(Write_10101), .out6(Write_10110), .out7(Write_10111), .in(demultiplexer_1_out2), .sel(A3[2:0]));  // open: en
  Demultiplexer #(.select(3)) demultiplexer_5 (
    .out0(Write_11000), .out1(Write_11001), .out2(Write_11010), .out3(Write_11011), .out4(Write_11100),
    .out5(Write_11101), .out6(Write_11110), .out7(Write_11111), .in(demultiplexer_1_out3), .sel(A3[2:0]));  // open: en
  Multiplexer #(.select(3), .width(32)) multiplexer_1 (
    .in0(Read_00000), .in1(Read_00001), .in2(Read_00010), .in3(Read_00011), .in4(Read_00100),
    .in5(Read_00101), .in6(Read_00110), .in7(Read_00111), .out(multiplexer_1_out), .sel(A1[2:0]));  // open: en
  Multiplexer #(.select(3), .width(32)) multiplexer_2 (
    .in0(Read_01000), .in1(Read_01001), .in2(Read_01010), .in3(Read_01011), .in4(Read_01100),
    .in5(Read_01101), .in6(Read_01110), .in7(Read_01111), .out(multiplexer_2_out), .sel(A1[2:0]));  // open: en
  Multiplexer #(.select(3), .width(32)) multiplexer_3 (
    .in0(Read_10000), .in1(Read_10001), .in2(Read_10010), .in3(Read_10011), .in4(Read_10100),
    .in5(Read_10101), .in6(Read_10110), .in7(Read_10111), .out(multiplexer_3_out), .sel(A1[2:0]));  // open: en
  Multiplexer #(.select(3), .width(32)) multiplexer_4 (
    .in0(Read_11000), .in1(Read_11001), .in2(Read_11010), .in3(Read_11011), .in4(Read_11100),
    .in5(Read_11101), .in6(Read_11110), .in7(Read_11111), .out(multiplexer_4_out), .sel(A1[2:0]));  // open: en
  Register #(.width(32)) register_9 (.D(WD), .en(Write_01000), .Q(Read_01000), .clk(clk), .clr(reset));
  Register #(.width(32)) register_10 (.D(WD), .en(Write_01001), .Q(Read_01001), .clk(clk), .clr(reset));
  Register #(.width(32)) register_11 (.D(WD), .en(Write_01010), .Q(Read_01010), .clk(clk), .clr(reset));
  Register #(.width(32)) register_12 (.D(WD), .en(Write_01011), .Q(Read_01011), .clk(clk), .clr(reset));
  Register #(.width(32)) register_13 (.D(WD), .en(Write_01100), .Q(Read_01100), .clk(clk), .clr(reset));
  Register #(.width(32)) register_14 (.D(WD), .en(Write_01101), .Q(Read_01101), .clk(clk), .clr(reset));
  Register #(.width(32)) register_15 (.D(WD), .en(Write_01110), .Q(Read_01110), .clk(clk), .clr(reset));
  Register #(.width(32)) register_16 (.D(WD), .en(Write_01111), .Q(Read_01111), .clk(clk), .clr(reset));
  Multiplexer #(.select(2), .width(32)) multiplexer_5 (
    .in0(multiplexer_1_out), .in1(multiplexer_2_out), .in2(multiplexer_3_out), .in3(multiplexer_4_out),
    .out(RD1), .sel(A1[4:3]));  // open: en
  Register #(.width(32)) register_17 (.D(WD), .en(Write_10000), .Q(Read_10000), .clk(clk), .clr(reset));
  Register #(.width(32)) register_18 (.D(WD), .en(Write_10001), .Q(Read_10001), .clk(clk), .clr(reset));
  Register #(.width(32)) register_19 (.D(WD), .en(Write_10010), .Q(Read_10010), .clk(clk), .clr(reset));
  Register #(.width(32)) register_20 (.D(WD), .en(Write_10011), .Q(Read_10011), .clk(clk), .clr(reset));
  Register #(.width(32)) register_21 (.D(WD), .en(Write_10100), .Q(Read_10100), .clk(clk), .clr(reset));
  Register #(.width(32)) register_22 (.D(WD), .en(Write_10101), .Q(Read_10101), .clk(clk), .clr(reset));
  Register #(.width(32)) register_23 (.D(WD), .en(Write_10110), .Q(Read_10110), .clk(clk), .clr(reset));
  Register #(.width(32)) register_24 (.D(WD), .en(Write_10111), .Q(Read_10111), .clk(clk), .clr(reset));
  Multiplexer #(.select(3), .width(32)) multiplexer_6 (
    .in0(Read_00000), .in1(Read_00001), .in2(Read_00010), .in3(Read_00011), .in4(Read_00100),
    .in5(Read_00101), .in6(Read_00110), .in7(Read_00111), .out(multiplexer_6_out), .sel(A2[2:0]));  // open: en
  Multiplexer #(.select(3), .width(32)) multiplexer_7 (
    .in0(Read_01000), .in1(Read_01001), .in2(Read_01010), .in3(Read_01011), .in4(Read_01100),
    .in5(Read_01101), .in6(Read_01110), .in7(Read_01111), .out(multiplexer_7_out), .sel(A2[2:0]));  // open: en
  Multiplexer #(.select(3), .width(32)) multiplexer_8 (
    .in0(Read_10000), .in1(Read_10001), .in2(Read_10010), .in3(Read_10011), .in4(Read_10100),
    .in5(Read_10101), .in6(Read_10110), .in7(Read_10111), .out(multiplexer_8_out), .sel(A2[2:0]));  // open: en
  Multiplexer #(.select(3), .width(32)) multiplexer_9 (
    .in0(Read_11000), .in1(Read_11001), .in2(Read_11010), .in3(Read_11011), .in4(Read_11100),
    .in5(Read_11101), .in6(Read_11110), .in7(Read_11111), .out(multiplexer_9_out), .sel(A2[2:0]));  // open: en
  Register #(.width(32)) register_25 (.D(WD), .en(Write_11000), .Q(Read_11000), .clk(clk), .clr(reset));
  Register #(.width(32)) register_26 (.D(WD), .en(Write_11001), .Q(Read_11001), .clk(clk), .clr(reset));
  Register #(.width(32)) register_27 (.D(WD), .en(Write_11010), .Q(Read_11010), .clk(clk), .clr(reset));
  Register #(.width(32)) register_28 (.D(WD), .en(Write_11011), .Q(Read_11011), .clk(clk), .clr(reset));
  Register #(.width(32)) register_29 (.D(WD), .en(Write_11100), .Q(Read_11100), .clk(clk), .clr(reset));
  Register #(.width(32)) register_30 (.D(WD), .en(Write_11101), .Q(Read_11101), .clk(clk), .clr(reset));
  Register #(.width(32)) register_31 (.D(WD), .en(Write_11110), .Q(Read_11110), .clk(clk), .clr(reset));
  Register #(.width(32)) register_32 (.D(WD), .en(Write_11111), .Q(Read_11111), .clk(clk), .clr(reset));
  Multiplexer #(.select(2), .width(32)) multiplexer_10 (
    .in0(multiplexer_6_out), .in1(multiplexer_7_out), .in2(multiplexer_8_out), .in3(multiplexer_9_out),
    .out(RD2), .sel(A2[4:3]));  // open: en
endmodule

module ALU (
  input  [2:0] ALUOp,
  input  [31:0] A,
  input  [31:0] B,
  output Zero,
  output LessZero,
  output [31:0] C
);

  wire [31:0] adder_1_out, or_1_out, shifter_1_out, shifter_2_out, subtractor_1_out;

  Comparator #(.width(32)) comparator_1 (.a(A), .b(B), .eq(Zero), .lt(LessZero));  // open: gt
  Adder #(.width(32)) adder_1 (.a(A), .b(B), .out(adder_1_out));  // open: cin, cout
  Subtractor #(.width(32)) subtractor_1 (.a(A), .b(B), .out(subtractor_1_out));  // open: bin, bout
  assign or_1_out = A | B;  // OR_Gate or_1, 32 bits wide
  Shifter #(.width(32)) shifter_1 (.in(A), .\dist (B[4:0]), .out(shifter_1_out));
  Shifter #(.width(32)) shifter_2 (.in(B), .\dist (A[10:6]), .out(shifter_2_out));
  Multiplexer #(.select(3), .width(32)) multiplexer_1 (
    .in0(adder_1_out), .in1(subtractor_1_out), .in2(or_1_out), .in3(shifter_1_out), .in4({B[15:0], A[15:0]}),
    .in5(shifter_2_out), .out(C), .sel(ALUOp));  // open: in6, in7, en

  // Notes on the sheet:
  //   000
  //   001
  //   010
  //   011
  //   [lui]100
  //   [sll]101
endmodule

module IM (
  input  [31:0] PC,
  output [31:0] Instr
);

  ROM #(.addrWidth(5), .dataWidth(32)) rom_1 (.addr(PC[6:2]), .data(Instr));  // open: sel

  // Notes on the sheet:
  //   contents of rom_1 (hex, n*v repeats v):
  //   3c01000b 3421000a ac010000 80020000 80030002
endmodule

module DM (
  input  [31:0] Addr,
  input  [31:0] WD,
  input  DMWrite,
  input  clk,
  input  reset,
  input  [1:0] DMOp,
  output [31:0] RD
);

  wire [7:0] DM0_7, DM8_15, DM16_23, DM24_31, multiplexer_5_out;
  wire [15:0] multiplexer_4_out;
  wire [31:0] bit_extender_1_out, bit_extender_2_out, InData, multiplexer_1_out, multiplexer_2_out;

  Multiplexer #(.width(32)) multiplexer_1 (
    .in0({DM24_31, DM16_23, WD[15:0]}), .in1({WD[31:16], DM8_15, DM0_7}), .out(multiplexer_1_out),
    .sel(Addr[1]));  // open: en
  Multiplexer #(.select(2), .width(32)) multiplexer_2 (
    .in0({DM24_31, DM16_23, DM8_15, WD[7:0]}), .in1({DM24_31, DM16_23, WD[15:8], DM0_7}),
    .in2({DM24_31, WD[23:16], DM8_15, DM0_7}), .in3({WD[31:24], DM16_23, DM8_15, DM0_7}),
    .out(multiplexer_2_out), .sel(Addr[1:0]));  // open: en
  Multiplexer #(.select(2), .width(32)) multiplexer_3 (
    .in0(WD), .in1(multiplexer_1_out), .in2(multiplexer_2_out), .out(InData), .sel(DMOp));  // open: in3, en
  assign bit_extender_1_out = {{16{multiplexer_4_out[15]}}, multiplexer_4_out};  // Bit_Extender bit_extender_1
  Multiplexer #(.width(16)) multiplexer_4 (
    .in0({DM8_15, DM0_7}), .in1({DM24_31, DM16_23}), .out(multiplexer_4_out), .sel(Addr[1]));  // open: en
  assign bit_extender_2_out = {{24{multiplexer_5_out[7]}}, multiplexer_5_out};  // Bit_Extender bit_extender_2
  Multiplexer #(.select(2), .width(8)) multiplexer_5 (
    .in0(DM0_7), .in1(DM8_15), .in2(DM16_23), .in3(DM24_31), .out(multiplexer_5_out), .sel(Addr[1:0]));  // open: en
  RAM #(.addrWidth(5), .dataWidth(32), .bus("separate")) ram_1 (
    .addr(Addr[6:2]), .din(InData), .data({DM24_31, DM16_23, DM8_15, DM0_7}), .str(DMWrite), .clk(clk),
    .clr(reset));  // open: sel, ld
  Multiplexer #(.select(2), .width(32)) multiplexer_6 (
    .in0({DM24_31, DM16_23, DM8_15, DM0_7}), .in1(bit_extender_1_out), .in2(bit_extender_2_out), .out(RD),
    .sel(DMOp));  // open: in3, en

  // Other names for the same wires on the sheet: WD0_7[7:0] = WD[7:0]; WD8_15[7:0] = WD[15:8];
  //   WD16_23[7:0] = WD[23:16]; WD24_31[7:0] = WD[31:24]; Address[31:0] = Addr
endmodule

module EXT (
  input  EXTOp,
  input  [15:0] Imm,
  output [31:0] Output
);

  wire [31:0] bit_extender_1_out, bit_extender_2_out;

  assign bit_extender_1_out = {{16{1'b0}}, Imm};  // Bit_Extender bit_extender_1
  assign bit_extender_2_out = {{16{Imm[15]}}, Imm};  // Bit_Extender bit_extender_2
  Multiplexer #(.width(32)) multiplexer_1 (
    .in0(bit_extender_1_out), .in1(bit_extender_2_out), .out(Output), .sel(EXTOp));  // open: en
endmodule

module NPC (
  input  [31:0] PC,
  input  Zero,
  input  [25:0] Imm,
  input  LessZero,
  input  [2:0] NPCOp,
  input  [31:0] rs,
  output [31:0] PC_4,
  output [31:0] NPC
);

  wire [31:0] adder_2_out, bit_extender_1_out, multiplexer_1_out;

  Adder #(.width(32)) adder_1 (.a(32'h4), .b(PC), .out(PC_4));  // open: cin, cout
  assign bit_extender_1_out = {{14{Imm[15]}}, {Imm[15:0], 2'b00}};  // Bit_Extender bit_extender_1
  Adder #(.width(32)) adder_2 (.a(PC_4), .b(bit_extender_1_out), .out(adder_2_out));  // open: cin, cout
  Multiplexer #(.width(32)) multiplexer_1 (
    .in0(PC_4), .in1(adder_2_out), .out(multiplexer_1_out), .sel(Zero));  // open: en
  Multiplexer #(.select(3), .width(32)) multiplexer_2 (
    .in0(PC_4), .in1(multiplexer_1_out), .in6({PC[31:28], Imm, 2'b00}), .in7(rs), .out(NPC), .sel(NPCOp));  // open: in2, in3, in4, in5, en

  // Notes on the sheet:
  //   beq
  //   Ready for bltz, bgtz
  //   j, jal
  //   jalr, jr
  //   110
  //   111
  //   000
  //   001
endmodule

module CTRL (
  input  [5:0] opcode,
  input  [5:0] funct,
  output [1:0] WRA3Sel,
  output [1:0] WDSel,
  output [2:0] ALUOp,
  output [1:0] DMOp,
  output [2:0] NPCOp,
  output EXTOp,
  output WE,
  output ALUBSel,
  output DMWr,
  output ALUASel
);

  wire and_1_out, and_2_out, and_3_out, and_4_out, and_5_out, and_6_out, and_7_out, and_8_out, and_9_out,
       and_10_out, and_11_out, and_12_out, and_13_out, and_14_out, and_15_out, and_16_out, not_1_out,
       not_2_out, not_3_out, not_4_out, not_5_out, not_6_out, not_7_out, not_8_out, not_9_out, not_10_out,
       not_11_out, not_12_out, pull_resistor_1_node;

  not not_1 (not_1_out, opcode[5]);
  not not_2 (not_2_out, opcode[4]);
  not not_3 (not_3_out, opcode[3]);
  not not_4 (not_4_out, opcode[2]);
  not not_5 (not_5_out, opcode[1]);
  not not_6 (not_6_out, opcode[0]);
  not not_7 (not_7_out, funct[5]);
  not not_8 (not_8_out, funct[4]);
  not not_9 (not_9_out, funct[3]);
  not not_10 (not_10_out, funct[1]);
  not not_11 (not_11_out, funct[2]);
  not not_12 (not_12_out, funct[0]);
  and and_1 (and_1_out, not_1_out, not_2_out, not_3_out, not_4_out, not_5_out, not_6_out);
  and and_2 (and_2_out, funct[5], not_8_out, not_9_out, not_11_out, not_10_out, funct[0]);
  and and_3 (and_3_out, funct[5], not_8_out, not_9_out, not_11_out, funct[1], funct[0]);
  and and_4 (and_4_out, not_1_out, not_2_out, opcode[3], opcode[2], not_5_out, opcode[0]);
  and and_5 (and_5_out, opcode[5], not_2_out, not_3_out, not_4_out, opcode[1], opcode[0]);
  and and_6 (and_6_out, opcode[5], not_2_out, opcode[3], not_4_out, opcode[1], opcode[0]);
  and and_7 (and_7_out, not_1_out, not_2_out, not_3_out, opcode[2], not_5_out, not_6_out);
  and and_8 (and_8_out, not_1_out, not_2_out, opcode[3], opcode[2], opcode[1], opcode[0]);
  and and_9 (and_9_out, not_7_out, not_8_out, not_9_out, not_11_out, not_10_out, not_12_out);
  and and_10 (and_10_out, not_1_out, not_2_out, not_3_out, not_4_out, opcode[1], opcode[0]);
  and and_11 (and_11_out, not_7_out, not_8_out, not_11_out, not_10_out, not_12_out, funct[3]);
  and and_12 (and_12_out, opcode[5], not_2_out, not_3_out, not_4_out, not_5_out, not_6_out);
  Pull_Resistor pull_resistor_1 (.node(pull_resistor_1_node));
  and and_13 (and_13_out, and_1_out, and_2_out);
  and and_14 (and_14_out, and_1_out, and_3_out);
  and and_15 (and_15_out, and_1_out, and_9_out);
  and and_16 (and_16_out, and_1_out, and_11_out);
  or or_1 (NPCOp[2], pull_resistor_1_node, and_10_out, and_16_out);
  or or_2 (NPCOp[1], pull_resistor_1_node, and_10_out, and_16_out);
  or or_3 (NPCOp[0], pull_resistor_1_node, and_7_out, and_16_out);
  or or_4 (WRA3Sel[1], pull_resistor_1_node, and_10_out, and_16_out);
  or or_5 (WRA3Sel[0], pull_resistor_1_node, and_4_out, and_5_out, and_6_out, and_8_out, and_12_out);
  or or_6 (WDSel[1], pull_resistor_1_node, and_10_out, and_16_out);
  or or_7 (WDSel[0], pull_resistor_1_node, and_13_out, and_14_out, and_4_out, and_8_out, and_15_out);
  or or_8 (EXTOp, pull_resistor_1_node, and_5_out, and_6_out, and_12_out);
  or or_9 (WE, and_16_out, and_5_out, and_8_out, pull_resistor_1_node, and_13_out, and_14_out, and_4_out, and_5_out, and_15_out, and_10_out, and_12_out);
  or or_10 (ALUBSel, pull_resistor_1_node, and_4_out, and_5_out, and_6_out, and_8_out, and_12_out);
  or or_11 (ALUOp[2], pull_resistor_1_node, and_8_out, and_15_out);
  or or_12 (ALUOp[1], pull_resistor_1_node, and_4_out);
  or or_13 (ALUOp[0], pull_resistor_1_node, and_14_out, and_7_out, and_15_out);
  or or_14 (DMWr, pull_resistor_1_node, and_6_out);
  or or_15 (DMOp[0], pull_resistor_1_node, and_12_out);
  buf or_16 (DMOp[1], pull_resistor_1_node);  // OR_Gate
  or or_17 (ALUASel, pull_resistor_1_node, and_15_out);

  // Notes on the sheet:
  //   special
  //   addu
  //   subu
  //   ori
  //   lw
  //   sw
  //   jr
  //   beq
  //   lui
  //   sll
  //   jal
  //   lb
endmodule
