// Logisim project Logisim_1BitSwap.circ as structural Verilog: 1 circuit, main circuit 1bit-swap
module _1bit_swap (
  input  in_1,
  input  S,
  input  in_2,
  output out_2,
  output out_1
);

  wire and_1_out, and_2_out, and_3_out, and_4_out, nS_out;

  not nS (nS_out, S);
  and and_1 (and_1_out, nS_out, in_2);
  and and_2 (and_2_out, S, in_1);
  and and_3 (and_3_out, in_2, S);
  and and_4 (and_4_out, in_1, nS_out);
  or or_1 (out_2, and_1_out, and_2_out);
  or or_2 (out_1, and_3_out, and_4_out);
endmodule
