// Logisim project Logisim_4BitSort.circ as structural Verilog: 3 circuits, main circuit 1bit-swap
module _1bit_swap (
  input  in_1,
  input  S,
  input  in_2,
  output out_2,
  output out_1
);

  wire and_1_out, and_2_out, and_3_out, and_4_out, nS_out;

  not nS (nS_out, S);
  and and_1 (and_1_out, nS_out, in_2);
  and and_2 (and_2_out, S, in_1);
  and and_3 (and_3_out, in_2, S);
  and and_4 (and_4_out, in_1, nS_out);
  or or_1 (out_2, and_1_out, and_2_out);
  or or_2 (out_1, and_3_out, and_4_out);
endmodule

module _4bit_swap (
  input  S,
  input  [3:0] in_1,
  input  [3:0] in_2,
  output [3:0] out_1,
  output [3:0] out_2
);

  _1bit_swap u_1bit_swap_1 (.in_1(in_1[0]), .S(S), .in_2(in_2[0]), .out_2(out_2[0]), .out_1(out_1[0]));
  _1bit_swap u_1bit_swap_2 (.in_1(in_1[1]), .S(S), .in_2(in_2[1]), .out_2(out_2[1]), .out_1(out_1[1]));
  _1bit_swap u_1bit_swap_3 (.in_1(in_1[2]), .S(S), .in_2(in_2[2]), .out_2(out_2[2]), .out_1(out_1[2]));
  _1bit_swap u_1bit_swap_4 (.in_1(in_1[3]), .S(S), .in_2(in_2[3]), .out_2(out_2[3]), .out_1(out_1[3]));

  // Notes on the sheet:
  //   in_1_bit0
  //   in_2_bit0
  //   in_1_bit1
  //   in_2_bit1
  //   in_1_bit2
  //   in_2_bit2
  //   in_1_bit3
  //   in_2_bit3
  //   out_1_bit0
  //   out_1_bit1
  //   out_1_bit2
  //   out_1_bit3
  //   out_2_bit0
  //   out_2_bit1
  //   out_2_bit2
  //   out_2_bit3
endmodule

module _4bit_sort (
  input  [3:0] in_1,
  input  [3:0] in_2,
  input  [3:0] in_3,
  input  [3:0] in_4,
  output [3:0] out_1,
  output [3:0] out_2,
  output [3:0] out_3,
  output [3:0] out_4
);

  wire comparator_1_gt, comparator_2_gt, comparator_3_gt, comparator_4_gt, comparator_5_gt;
  wire [3:0] n4bit_swap_1_out_1, n4bit_swap_1_out_2, n4bit_swap_2_out_1, n4bit_swap_2_out_2,
       n4bit_swap_3_out_2, n4bit_swap_4_out_1;

  Comparator #(.width(4), .mode("unsigned")) comparator_1 (.a(in_1), .b(in_2), .gt(comparator_1_gt));  // open: eq, lt
  _4bit_swap u_4bit_swap_1 (
    .S(comparator_1_gt), .in_1(in_1), .in_2(in_2), .out_1(n4bit_swap_1_out_1), .out_2(n4bit_swap_1_out_2));
  _4bit_swap u_4bit_swap_2 (
    .S(comparator_2_gt), .in_1(in_3), .in_2(in_4), .out_1(n4bit_swap_2_out_1), .out_2(n4bit_swap_2_out_2));
  Comparator #(.width(4), .mode("unsigned")) comparator_2 (.a(in_3), .b(in_4), .gt(comparator_2_gt));  // open: eq, lt
  Comparator #(.width(4), .mode("unsigned")) comparator_3 (
    .a(n4bit_swap_1_out_1), .b(n4bit_swap_2_out_1), .gt(comparator_3_gt));  // open: eq, lt
  _4bit_swap u_4bit_swap_3 (
    .S(comparator_3_gt), .in_1(n4bit_swap_1_out_1), .in_2(n4bit_swap_2_out_1), .out_1(out_1),
    .out_2(n4bit_swap_3_out_2));
  _4bit_swap u_4bit_swap_4 (
    .S(comparator_4_gt), .in_1(n4bit_swap_1_out_2), .in_2(n4bit_swap_2_out_2), .out_1(n4bit_swap_4_out_1),
    .out_2(out_4));
  Comparator #(.width(4), .mode("unsigned")) comparator_4 (
    .a(n4bit_swap_1_out_2), .b(n4bit_swap_2_out_2), .gt(comparator_4_gt));  // open: eq, lt
  Comparator #(.width(4), .mode("unsigned")) comparator_5 (
    .a(n4bit_swap_3_out_2), .b(n4bit_swap_4_out_1), .gt(comparator_5_gt));  // open: eq, lt
  _4bit_swap u_4bit_swap_5 (
    .S(comparator_5_gt), .in_1(n4bit_swap_3_out_2), .in_2(n4bit_swap_4_out_1), .out_1(out_2), .out_2(out_3));

  // Notes on the sheet:
  //   minimum
  //   compare the middle two data
  //   maximum
endmodule
