// Logisim project Logisim_fibonacci.circ as structural Verilog: 3 circuits, main circuit main
module main (
  input  [2:0] in_2,
  output [3:0] out_2
);

  wire clock_1_out, next_status_1_s_out_0, next_status_1_s_out_1, next_status_1_s_out_2, register_1_q,
       register_2_q, register_3_q;

  next_status next_status_1 (
    .in_bit0(in_2[2]), .in_bit1(in_2[1]), .in_bit2(in_2[0]), .s_in_0(register_1_q), .s_in_1(register_2_q),
    .s_in_2(register_3_q), .s_out_0(next_status_1_s_out_0), .s_out_1(next_status_1_s_out_1),
    .s_out_2(next_status_1_s_out_2));
  Register #(.width(1)) register_1 (.D(next_status_1_s_out_0), .Q(register_1_q), .clk(clock_1_out));  // open: en, clr
  Register #(.width(1)) register_2 (.D(next_status_1_s_out_1), .Q(register_2_q), .clk(clock_1_out));  // open: en, clr
  Register #(.width(1)) register_3 (.D(next_status_1_s_out_2), .Q(register_3_q), .clk(clock_1_out));  // open: en, clr
  Clock clock_1 (.out(clock_1_out));
  \output  output_1 (
    .in_bit0(in_2[2]), .in_bit1(in_2[1]), .in_bit2(in_2[0]), .s_in_bit0(register_1_q),
    .s_in_bit1(register_2_q), .s_in_bit2(register_3_q), .out_bit0(out_2[0]), .out_bit1(out_2[1]),
    .out_bit2(out_2[2]), .out_bit3(out_2[3]));

  // Notes on the sheet:
  //   in_0
  //   in_1
  //   next_status
  //   output
endmodule

module next_status (
  input  in_bit0,
  input  in_bit1,
  input  in_bit2,
  input  s_in_0,
  input  s_in_1,
  input  s_in_2,
  output s_out_0,
  output s_out_1,
  output s_out_2
);

  wire and_1_out, and_2_out, and_3_out, and_4_out, and_5_out, and_6_out, and_7_out, and_8_out, and_9_out,
       and_10_out, and_11_out, and_12_out, and_13_out, and_14_out, and_15_out, and_16_out, and_17_out,
       and_18_out, and_19_out, and_20_out, and_21_out, and_22_out, and_23_out, and_24_out, not_1_out,
       not_2_out, not_3_out, not_4_out, not_5_out, not_6_out, not_7_out, not_8_out, not_9_out, not_10_out,
       not_11_out, not_12_out, not_13_out, not_14_out, not_15_out, not_16_out, not_17_out, or_1_out,
       or_3_out, or_4_out, or_5_out, or_6_out, or_8_out, or_9_out;

  not not_1 (not_1_out, in_bit1);
  not not_2 (not_2_out, in_bit2);
  not not_3 (not_3_out, s_in_1);
  not not_4 (not_4_out, s_in_0);
  not not_5 (not_5_out, s_in_1);
  not not_6 (not_6_out, in_bit1);
  not not_7 (not_7_out, in_bit2);
  not not_8 (not_8_out, in_bit0);
  not not_9 (not_9_out, s_in_1);
  and and_1 (and_1_out, in_bit2, s_in_1);
  and and_2 (and_2_out, and_1_out, s_in_2);
  and and_3 (and_3_out, in_bit1, s_in_1);
  and and_4 (and_4_out, not_1_out, not_2_out);
  not not_10 (not_10_out, s_in_2);
  and and_5 (and_5_out, in_bit1, in_bit2);
  and and_6 (and_6_out, not_3_out, s_in_2);
  and and_7 (and_7_out, in_bit0, not_4_out);
  and and_8 (and_8_out, not_5_out, s_in_2);
  and and_9 (and_9_out, not_6_out, not_7_out);
  not not_11 (not_11_out, in_bit2);
  not not_12 (not_12_out, in_bit0);
  not not_13 (not_13_out, in_bit1);
  and and_10 (and_10_out, not_8_out, in_bit1);
  not not_14 (not_14_out, in_bit2);
  and and_11 (and_11_out, in_bit1, not_9_out);
  not not_15 (not_15_out, s_in_2);
  not not_16 (not_16_out, s_in_0);
  or or_1 (or_1_out, s_in_0, and_2_out);
  and and_12 (and_12_out, and_3_out, s_in_2);
  and and_13 (and_13_out, and_4_out, s_in_1);
  and and_14 (and_14_out, s_in_1, not_10_out);
  and and_15 (and_15_out, and_5_out, and_6_out);
  and and_16 (and_16_out, and_7_out, and_8_out);
  and and_17 (and_17_out, and_9_out, s_in_1);
  and and_18 (and_18_out, not_11_out, s_in_0);
  and and_19 (and_19_out, not_12_out, not_13_out);
  and and_20 (and_20_out, and_10_out, not_14_out);
  and and_21 (and_21_out, and_11_out, not_15_out);
  and and_22 (and_22_out, in_bit0, not_16_out);
  not not_17 (not_17_out, s_in_2);
  or or_2 (s_out_0, or_1_out, and_12_out);
  or or_3 (or_3_out, and_13_out, and_14_out);
  or or_4 (or_4_out, and_15_out, and_16_out);
  or or_5 (or_5_out, and_17_out, and_18_out);
  and and_23 (and_23_out, and_19_out, in_bit2);
  or or_6 (or_6_out, and_20_out, and_21_out);
  and and_24 (and_24_out, and_22_out, not_17_out);
  or or_7 (s_out_1, or_3_out, or_4_out);
  or or_8 (or_8_out, or_5_out, and_23_out);
  or or_9 (or_9_out, or_6_out, and_24_out);
  or or_10 (s_out_2, or_8_out, or_9_out);
endmodule

module \output  (
  input  in_bit0,
  input  in_bit1,
  input  in_bit2,
  input  s_in_bit0,
  input  s_in_bit1,
  input  s_in_bit2,
  output out_bit0,
  output out_bit1,
  output out_bit2,
  output out_bit3
);

  wire and_1_out, and_2_out, and_3_out, and_4_out, and_5_out, and_6_out, and_7_out, and_8_out, and_9_out,
       and_10_out, and_11_out, and_12_out, and_13_out, and_14_out, and_15_out, and_16_out, and_17_out,
       and_18_out, and_19_out, and_20_out, and_21_out, and_22_out, and_23_out, and_24_out, and_25_out,
       and_26_out, and_27_out, and_28_out, and_29_out, and_30_out, and_31_out, and_32_out, and_33_out,
       and_34_out, and_35_out, and_36_out, and_37_out, and_38_out, and_39_out, and_40_out, and_41_out,
       and_42_out, and_43_out, and_44_out, and_45_out, and_46_out, and_47_out, and_48_out, and_49_out,
       and_50_out, and_51_out, and_52_out, and_53_out, and_54_out, and_55_out, and_56_out, and_57_out,
       and_58_out, and_59_out, and_60_out, and_61_out, and_62_out, and_63_out, and_64_out, not_1_out,
       not_2_out, not_3_out, not_4_out, not_5_out, not_6_out, not_7_out, not_8_out, not_9_out, not_10_out,
       not_11_out, not_12_out, not_13_out, not_14_out, not_15_out, not_16_out, not_17_out, not_18_out,
       not_19_out, not_20_out, not_21_out, not_22_out, not_23_out, not_24_out, not_25_out, not_26_out,
       not_27_out, not_28_out, not_29_out, or_2_out, or_3_out, or_4_out, or_5_out, or_7_out;

  not not_1 (not_1_out, in_bit0);
  not not_2 (not_2_out, in_bit1);
  not not_3 (not_3_out, s_in_bit0);
  not not_4 (not_4_out, s_in_bit1);
  not not_5 (not_5_out, in_bit0);
  not not_6 (not_6_out, s_in_bit0);
  not not_7 (not_7_out, s_in_bit1);
  not not_8 (not_8_out, in_bit1);
  not not_9 (not_9_out, s_in_bit1);
  not not_10 (not_10_out, s_in_bit1);
  not not_11 (not_11_out, in_bit0);
  not not_12 (not_12_out, s_in_bit0);
  not not_13 (not_13_out, in_bit1);
  not not_14 (not_14_out, s_in_bit0);
  not not_15 (not_15_out, in_bit1);
  not not_16 (not_16_out, s_in_bit1);
  not not_17 (not_17_out, s_in_bit1);
  and and_1 (and_1_out, in_bit0, in_bit1);
  not not_18 (not_18_out, s_in_bit1);
  and and_2 (and_2_out, in_bit0, in_bit1);
  and and_3 (and_3_out, s_in_bit0, s_in_bit1);
  not not_19 (not_19_out, s_in_bit2);
  and and_4 (and_4_out, not_1_out, not_2_out);
  and and_5 (and_5_out, not_3_out, not_4_out);
  and and_6 (and_6_out, not_5_out, in_bit1);
  not not_20 (not_20_out, in_bit2);
  and and_7 (and_7_out, not_6_out, not_7_out);
  not not_21 (not_21_out, in_bit1);
  not not_22 (not_22_out, s_in_bit0);
  and and_8 (and_8_out, in_bit0, not_8_out);
  and and_9 (and_9_out, s_in_bit0, not_9_out);
  not not_23 (not_23_out, s_in_bit2);
  and and_10 (and_10_out, in_bit0, in_bit1);
  and and_11 (and_11_out, s_in_bit0, not_10_out);
  and and_12 (and_12_out, not_11_out, in_bit1);
  and and_13 (and_13_out, not_12_out, s_in_bit1);
  not not_24 (not_24_out, s_in_bit2);
  and and_14 (and_14_out, in_bit0, not_13_out);
  not not_25 (not_25_out, in_bit2);
  and and_15 (and_15_out, not_14_out, s_in_bit1);
  and and_16 (and_16_out, in_bit0, not_15_out);
  and and_17 (and_17_out, s_in_bit0, not_16_out);
  not not_26 (not_26_out, s_in_bit2);
  and and_18 (and_18_out, in_bit0, in_bit1);
  and and_19 (and_19_out, s_in_bit0, not_17_out);
  and and_20 (and_20_out, and_1_out, s_in_bit0);
  and and_21 (and_21_out, not_18_out, s_in_bit2);
  and and_22 (and_22_out, and_2_out, in_bit2);
  and and_23 (and_23_out, and_3_out, not_19_out);
  and and_24 (and_24_out, and_4_out, in_bit2);
  and and_25 (and_25_out, and_5_out, s_in_bit2);
  and and_26 (and_26_out, and_6_out, not_20_out);
  and and_27 (and_27_out, and_7_out, s_in_bit2);
  and and_28 (and_28_out, in_bit0, not_21_out);
  not not_27 (not_27_out, in_bit2);
  and and_29 (and_29_out, not_22_out, s_in_bit1);
  and and_30 (and_30_out, and_8_out, in_bit2);
  and and_31 (and_31_out, and_9_out, not_23_out);
  and and_32 (and_32_out, and_10_out, in_bit2);
  and and_33 (and_33_out, and_11_out, s_in_bit2);
  and and_34 (and_34_out, in_bit0, in_bit1);
  and and_35 (and_35_out, s_in_bit0, s_in_bit1);
  not not_28 (not_28_out, s_in_bit2);
  and and_36 (and_36_out, and_12_out, in_bit2);
  and and_37 (and_37_out, and_13_out, not_24_out);
  and and_38 (and_38_out, and_14_out, not_25_out);
  and and_39 (and_39_out, and_15_out, s_in_bit2);
  and and_40 (and_40_out, and_16_out, in_bit2);
  and and_41 (and_41_out, and_17_out, not_26_out);
  and and_42 (and_42_out, and_18_out, in_bit2);
  and and_43 (and_43_out, and_19_out, s_in_bit2);
  and and_44 (and_44_out, in_bit0, in_bit1);
  and and_45 (and_45_out, s_in_bit0, s_in_bit1);
  not not_29 (not_29_out, s_in_bit2);
  and and_46 (and_46_out, and_20_out, and_21_out);
  and and_47 (and_47_out, and_22_out, and_23_out);
  and and_48 (and_48_out, and_24_out, and_25_out);
  and and_49 (and_49_out, and_26_out, and_27_out);
  and and_50 (and_50_out, and_28_out, not_27_out);
  and and_51 (and_51_out, and_29_out, s_in_bit2);
  and and_52 (and_52_out, and_30_out, and_31_out);
  and and_53 (and_53_out, and_32_out, and_33_out);
  and and_54 (and_54_out, and_34_out, in_bit2);
  and and_55 (and_55_out, and_35_out, not_28_out);
  and and_56 (and_56_out, and_36_out, and_37_out);
  and and_57 (and_57_out, and_38_out, and_39_out);
  and and_58 (and_58_out, and_40_out, and_41_out);
  and and_59 (and_59_out, and_42_out, and_43_out);
  and and_60 (and_60_out, and_44_out, in_bit2);
  and and_61 (and_61_out, and_45_out, not_29_out);
  or or_1 (out_bit3, and_46_out, and_47_out);
  or or_2 (or_2_out, and_48_out, and_49_out);
  or or_3 (or_3_out, or_2_out, and_62_out);
  and and_62 (and_62_out, and_50_out, and_51_out);
  or or_4 (or_4_out, and_52_out, and_53_out);
  or or_5 (or_5_out, or_4_out, and_63_out);
  and and_63 (and_63_out, and_54_out, and_55_out);
  or or_6 (out_bit1, and_56_out, and_57_out);
  or or_7 (or_7_out, and_58_out, and_59_out);
  or or_8 (out_bit2, or_7_out, and_64_out);
  and and_64 (and_64_out, and_60_out, and_61_out);
  or or_9 (out_bit0, or_3_out, or_5_out);
endmodule
