// Logisim project Logisim_fibonacci2.circ as structural Verilog: 4 circuits, main circuit main
module main (
  input  [31:0] \input ,
  output [31:0] \output 
);

  wire clock_1_out, counter_1_q, get_bit_1_halt_flag, get_bit_1_out_bit;
  wire [31:0] get_fib_matrix_1_fib_0_0, get_fib_matrix_1_fib_0_1, get_fib_matrix_1_fib_1_0,
       get_fib_matrix_1_fib_1_1, matrix_mul_1_c_0_0, matrix_mul_1_c_0_1, matrix_mul_1_c_1_0,
       matrix_mul_1_c_1_1, multiplexer_1_out, multiplexer_2_out, multiplexer_3_out, multiplexer_4_out,
       multiplexer_5_out, multiplexer_6_out, multiplexer_7_out, multiplexer_8_out, register_1_q,
       register_2_q, register_3_q, register_4_q;

  get_bit get_bit_1 (.\input (\input ), .halt_flag(get_bit_1_halt_flag), .out_bit(get_bit_1_out_bit));
  get_fib_matrix get_fib_matrix_1 (
    .Fib_0_0(get_fib_matrix_1_fib_0_0), .Fib_0_1(get_fib_matrix_1_fib_0_1),
    .Fib_1_0(get_fib_matrix_1_fib_1_0), .Fib_1_1(get_fib_matrix_1_fib_1_1), .sel(get_bit_1_out_bit));
  Multiplexer #(.width(32)) multiplexer_1 (
    .in0(get_fib_matrix_1_fib_0_0), .in1(32'h1), .out(multiplexer_1_out), .sel(get_bit_1_halt_flag));  // open: en
  Multiplexer #(.width(32)) multiplexer_2 (
    .in0(get_fib_matrix_1_fib_0_1), .in1({32{1'b0}}), .out(multiplexer_2_out), .sel(get_bit_1_halt_flag));  // open: en
  Multiplexer #(.width(32)) multiplexer_3 (
    .in0(get_fib_matrix_1_fib_1_0), .in1({32{1'b0}}), .out(multiplexer_3_out), .sel(get_bit_1_halt_flag));  // open: en
  Multiplexer #(.width(32)) multiplexer_4 (
    .in0(get_fib_matrix_1_fib_1_1), .in1(32'h1), .out(multiplexer_4_out), .sel(get_bit_1_halt_flag));  // open: en
  matrix_mul matrix_mul_1 (
    .A_0_0(multiplexer_1_out), .A_0_1(multiplexer_2_out), .A_1_0(multiplexer_3_out),
    .A_1_1(multiplexer_4_out), .B_0_0(multiplexer_5_out), .B_0_1(multiplexer_6_out),
    .B_1_0(multiplexer_7_out), .B_1_1(multiplexer_8_out), .C_0_0(matrix_mul_1_c_0_0),
    .C_0_1(matrix_mul_1_c_0_1), .C_1_0(matrix_mul_1_c_1_0), .C_1_1(matrix_mul_1_c_1_1));
  Clock clock_1 (.out(clock_1_out));
  Register #(.width(32)) register_1 (.D(matrix_mul_1_c_0_0), .Q(register_1_q), .clk(clock_1_out));  // open: en, clr
  Register #(.width(32)) register_2 (.D(matrix_mul_1_c_0_1), .Q(register_2_q), .clk(clock_1_out));  // open: en, clr
  Register #(.width(32)) register_3 (.D(matrix_mul_1_c_1_0), .Q(register_3_q), .clk(clock_1_out));  // open: en, clr
  Register #(.width(32)) register_4 (.D(matrix_mul_1_c_1_1), .Q(register_4_q), .clk(clock_1_out));  // open: en, clr
  Counter #(.width(1), .max('h1), .ongoal("stay")) counter_1 (
    .Q(counter_1_q), .clk(clock_1_out));  // open: load, D, count, carry, clr
  Multiplexer #(.width(32)) multiplexer_5 (
    .in0(32'h1), .in1(register_1_q), .out(multiplexer_5_out), .sel(counter_1_q));  // open: en
  Multiplexer #(.width(32)) multiplexer_6 (
    .in0({32{1'b0}}), .in1(register_2_q), .out(multiplexer_6_out), .sel(counter_1_q));  // open: en
  Multiplexer #(.width(32)) multiplexer_7 (
    .in0({32{1'b0}}), .in1(register_3_q), .out(multiplexer_7_out), .sel(counter_1_q));  // open: en
  Multiplexer #(.width(32)) multiplexer_8 (
    .in0(32'h1), .in1(register_4_q), .out(multiplexer_8_out), .sel(counter_1_q));  // open: en
  Multiplexer #(.width(32)) multiplexer_9 (
    .in0({32{1'b0}}), .in1(multiplexer_7_out), .out(\output ), .sel(get_bit_1_halt_flag));  // open: en

  // Notes on the sheet:
  //   每次得到输入数据的一位
  //   get_bit
  //   get_fib_matrix
  //   交给get_fib_matrix得到相应位的Fib矩阵
  //   matrix_mul
  //   与上一周期得到的结果相乘
  //   通过halt_flag信号判断是否处理完毕，未处理完输出0，否则输出结果
  //   为寄存器赋初始值
endmodule

module get_bit (
  input  [31:0] \input ,
  output halt_flag,
  output out_bit
);

  wire clock_1_out, counter_1_q;
  wire [5:0] counter_2_q;
  wire [31:0] multiplexer_1_out, register_1_q;
  wire [31:1] and_1_out;

  Multiplexer #(.width(32)) multiplexer_1 (
    .in0(\input ), .in1(register_1_q), .out(multiplexer_1_out), .sel(counter_1_q));  // open: en
  Counter #(.width(1), .max('h1), .ongoal("stay")) counter_1 (
    .Q(counter_1_q), .clk(clock_1_out));  // open: load, D, count, carry, clr
  Clock clock_1 (.out(clock_1_out));
  Register #(.width(32)) register_1 (
    .D({multiplexer_1_out[0], multiplexer_1_out[31:1]}), .Q(register_1_q), .clk(clock_1_out));  // open: en, clr
  // Probe on counter_2_q
  Counter #(.width(6), .max('h3f), .ongoal("stay")) counter_2 (
    .Q(counter_2_q), .clk(clock_1_out));  // open: load, D, count, carry, clr
  assign {and_1_out, out_bit} = 32'h1 & multiplexer_1_out;  // AND_Gate and_1, 32 bits wide
  Comparator #(.width(6), .mode("unsigned")) comparator_1 (
    .a(6'b011111), .b(counter_2_q), .lt(halt_flag));  // open: gt, eq

  // Notes on the sheet:
  //   使得数据左移一位
  //   计数器记录时钟周期数，大于32则处理完毕，halt_flag置为1
  //   每次给出最低位
endmodule

module matrix_mul (
  input  [31:0] A_0_0,
  input  [31:0] A_0_1,
  input  [31:0] A_1_0,
  input  [31:0] A_1_1,
  input  [31:0] B_0_0,
  input  [31:0] B_0_1,
  input  [31:0] B_1_0,
  input  [31:0] B_1_1,
  output [31:0] C_0_0,
  output [31:0] C_0_1,
  output [31:0] C_1_0,
  output [31:0] C_1_1
);

  wire [31:0] multiplier_1_out, multiplier_2_out, multiplier_3_out, multiplier_4_out, multiplier_5_out,
       multiplier_6_out, multiplier_7_out, multiplier_8_out;

  Multiplier #(.width(32)) multiplier_1 (.a(A_0_0), .b(B_0_0), .out(multiplier_1_out));  // open: cin, cout
  Multiplier #(.width(32)) multiplier_2 (.a(A_0_1), .b(B_1_0), .out(multiplier_2_out));  // open: cin, cout
  Multiplier #(.width(32)) multiplier_3 (.a(A_0_0), .b(B_0_1), .out(multiplier_3_out));  // open: cin, cout
  Multiplier #(.width(32)) multiplier_4 (.a(A_0_1), .b(B_1_1), .out(multiplier_4_out));  // open: cin, cout
  Multiplier #(.width(32)) multiplier_5 (.a(A_1_0), .b(B_0_0), .out(multiplier_5_out));  // open: cin, cout
  Multiplier #(.width(32)) multiplier_6 (.a(A_1_1), .b(B_1_0), .out(multiplier_6_out));  // open: cin, cout
  Multiplier #(.width(32)) multiplier_7 (.a(A_1_0), .b(B_0_1), .out(multiplier_7_out));  // open: cin, cout
  Multiplier #(.width(32)) multiplier_8 (.a(A_1_1), .b(B_1_1), .out(multiplier_8_out));  // open: cin, cout
  Adder #(.width(32)) adder_1 (.a(multiplier_1_out), .b(multiplier_2_out), .out(C_0_0));  // open: cin, cout
  Adder #(.width(32)) adder_2 (.a(multiplier_3_out), .b(multiplier_4_out), .out(C_0_1));  // open: cin, cout
  Adder #(.width(32)) adder_3 (.a(multiplier_5_out), .b(multiplier_6_out), .out(C_1_0));  // open: cin, cout
  Adder #(.width(32)) adder_4 (.a(multiplier_7_out), .b(multiplier_8_out), .out(C_1_1));  // open: cin, cout
endmodule

module get_fib_matrix (
  input  sel,
  output [31:0] Fib_0_0,
  output [31:0] Fib_0_1,
  output [31:0] Fib_1_0,
  output [31:0] Fib_1_1
);

  wire clock_1_out, counter_1_q, counter_2_q;
  wire [31:0] matrix_mul_1_c_0_0, matrix_mul_1_c_0_1, matrix_mul_1_c_1_0, matrix_mul_1_c_1_1,
       multiplexer_1_out, multiplexer_2_out, multiplexer_3_out, multiplexer_4_out, multiplexer_5_out,
       multiplexer_6_out, multiplexer_7_out, multiplexer_8_out, register_1_q, register_2_q, register_3_q,
       register_4_q;

  Multiplexer #(.width(32)) multiplexer_1 (
    .in0(32'h1), .in1(multiplexer_5_out), .out(multiplexer_1_out), .sel(counter_1_q));  // open: en
  Multiplexer #(.width(32)) multiplexer_2 (
    .in0(32'h1), .in1(multiplexer_6_out), .out(multiplexer_2_out), .sel(counter_1_q));  // open: en
  Multiplexer #(.width(32)) multiplexer_3 (
    .in0(32'h1), .in1(multiplexer_7_out), .out(multiplexer_3_out), .sel(counter_1_q));  // open: en
  Multiplexer #(.width(32)) multiplexer_4 (
    .in0({32{1'b0}}), .in1(multiplexer_8_out), .out(multiplexer_4_out), .sel(counter_1_q));  // open: en
  Counter #(.width(1), .max('h1), .ongoal("stay")) counter_1 (
    .Q(counter_1_q), .clk(clock_1_out));  // open: load, D, count, carry, clr
  matrix_mul matrix_mul_1 (
    .A_0_0(multiplexer_1_out), .A_0_1(multiplexer_2_out), .A_1_0(multiplexer_3_out),
    .A_1_1(multiplexer_4_out), .B_0_0(multiplexer_5_out), .B_0_1(multiplexer_6_out),
    .B_1_0(multiplexer_7_out), .B_1_1(multiplexer_8_out), .C_0_0(matrix_mul_1_c_0_0),
    .C_0_1(matrix_mul_1_c_0_1), .C_1_0(matrix_mul_1_c_1_0), .C_1_1(matrix_mul_1_c_1_1));
  Clock clock_1 (.out(clock_1_out));
  Register #(.width(32)) register_1 (.D(matrix_mul_1_c_0_0), .Q(register_1_q), .clk(clock_1_out));  // open: en, clr
  Register #(.width(32)) register_2 (.D(matrix_mul_1_c_0_1), .Q(register_2_q), .clk(clock_1_out));  // open: en, clr
  Register #(.width(32)) register_3 (.D(matrix_mul_1_c_1_0), .Q(register_3_q), .clk(clock_1_out));  // open: en, clr
  Register #(.width(32)) register_4 (.D(matrix_mul_1_c_1_1), .Q(register_4_q), .clk(clock_1_out));  // open: en, clr
  Counter #(.width(1), .max('h1), .ongoal("stay")) counter_2 (
    .Q(counter_2_q), .clk(clock_1_out));  // open: load, D, count, carry, clr
  Multiplexer #(.width(32)) multiplexer_5 (
    .in0(multiplexer_1_out), .in1(register_1_q), .out(multiplexer_5_out), .sel(counter_2_q));  // open: en
  Multiplexer #(.width(32)) multiplexer_6 (
    .in0(multiplexer_1_out), .in1(register_2_q), .out(multiplexer_6_out), .sel(counter_2_q));  // open: en
  Multiplexer #(.width(32)) multiplexer_7 (
    .in0(multiplexer_1_out), .in1(register_3_q), .out(multiplexer_7_out), .sel(counter_2_q));  // open: en
  Multiplexer #(.width(32)) multiplexer_8 (
    .in0(multiplexer_4_out), .in1(register_4_q), .out(multiplexer_8_out), .sel(counter_2_q));  // open: en
  Multiplexer #(.width(32)) multiplexer_9 (.in0(32'h1), .in1(multiplexer_5_out), .out(Fib_0_0), .sel(sel));  // open: en
  Multiplexer #(.width(32)) multiplexer_10 (
    .in0({32{1'b0}}), .in1(multiplexer_6_out), .out(Fib_0_1), .sel(sel));  // open: en
  Multiplexer #(.width(32)) multiplexer_11 (
    .in0({32{1'b0}}), .in1(multiplexer_7_out), .out(Fib_1_0), .sel(sel));  // open: en
  Multiplexer #(.width(32)) multiplexer_12 (
    .in0(32'h1), .in1(multiplexer_8_out), .out(Fib_1_1), .sel(sel));  // open: en

  // Notes on the sheet:
  //   矩阵乘法器
  //   每一次将上一周期得到的矩阵平方
  //   特判输出，如果这一位是0，那么给出单位阵，否则给出相应Fib矩阵
endmodule
