// Logisim project Logisim_mod5.circ as structural Verilog: 3 circuits, main circuit mod5
module mod5 (
  input  In,
  output out_2,
  output out_3,
  output out_4,
  output out_5,
  output out_6
);

  wire clock_1_out, counter_1_q, multiplexer_1_out, reg_s0_q, reg_s1_q, reg_s2_q, reg_s3_q, reg_s4_q;

  next_status next_status_1 (
    .In(In), .S_in_0(reg_s0_q), .S_in_1(multiplexer_1_out), .S_in_2(reg_s2_q), .S_in_3(reg_s3_q),
    .S_in_4(reg_s4_q), .S_out_0(out_2), .S_out_1(out_3), .S_out_2(out_4), .S_out_3(out_5), .S_out_4(out_6));
  Register #(.width(1)) reg_s0 (.D(out_2), .Q(reg_s0_q), .clk(clock_1_out));  // open: en, clr
  Register #(.width(1)) reg_s1 (.D(out_3), .Q(reg_s1_q), .clk(clock_1_out));  // open: en, clr
  Register #(.width(1)) reg_s2 (.D(out_4), .Q(reg_s2_q), .clk(clock_1_out));  // open: en, clr
  Register #(.width(1)) reg_s3 (.D(out_5), .Q(reg_s3_q), .clk(clock_1_out));  // open: en, clr
  Register #(.width(1)) reg_s4 (.D(out_6), .Q(reg_s4_q), .clk(clock_1_out));  // open: en, clr
  Clock clock_1 (.out(clock_1_out));
  Multiplexer multiplexer_1 (.in0(1'b1), .in1(reg_s1_q), .out(multiplexer_1_out), .sel(counter_1_q));  // open: en
  Counter #(.width(1), .max('h1), .ongoal("stay")) counter_1 (
    .Q(counter_1_q), .clk(clock_1_out));  // open: load, D, count, carry, clr
endmodule

module next_status (
  input  In,
  input  S_in_0,
  input  S_in_1,
  input  S_in_2,
  input  S_in_3,
  input  S_in_4,
  output S_out_0,
  output S_out_1,
  output S_out_2,
  output S_out_3,
  output S_out_4
);

  wire and_1_out, and_2_out, and_3_out, and_4_out, not_1_out, not_2_out, not_3_out, not_4_out, not_5_out,
       not_6_out, not_7_out, not_8_out, not_9_out, not_10_out;

  not not_1 (not_1_out, In);
  not not_2 (not_2_out, S_in_2);
  not not_3 (not_3_out, S_in_2);
  not not_4 (not_4_out, S_in_1);
  not not_5 (not_5_out, In);
  not not_6 (not_6_out, S_in_1);
  and and_1 (and_1_out, not_1_out, not_2_out);
  not not_7 (not_7_out, S_in_3);
  and and_2 (and_2_out, In, not_3_out);
  not not_8 (not_8_out, S_in_3);
  and and_3 (and_3_out, In, not_4_out);
  not not_9 (not_9_out, S_in_4);
  and and_4 (and_4_out, not_5_out, not_6_out);
  not not_10 (not_10_out, S_in_4);
  and and_5 (S_out_1, and_1_out, not_7_out);
  and and_6 (S_out_2, and_2_out, not_8_out);
  and and_7 (S_out_3, and_3_out, not_9_out);
  and and_8 (S_out_4, and_4_out, not_10_out);

  assign S_out_0 = 1'b0;
endmodule

module init_reg (
  input  in_1,
  output out_2
);

  wire clock_1_out, counter_1_q, register_1_q;

  Clock clock_1 (.out(clock_1_out));
  Register #(.width(1)) register_1 (.D(in_1), .Q(register_1_q), .clk(clock_1_out));  // open: en, clr
  Multiplexer multiplexer_1 (.in0(1'b1), .in1(register_1_q), .out(out_2), .sel(counter_1_q));  // open: en
  Counter #(.width(1), .max('h1), .ongoal("stay")) counter_1 (
    .Q(counter_1_q), .clk(clock_1_out));  // open: load, D, count, carry, clr
endmodule
