// Logisim project Logisim_vacation_judge.circ as structural Verilog: 1 circuit, main circuit main
module main (
  input  [3:0] in_1,
  output yes_no
);

  wire and_1_out, and_2_out, and_3_out, and_4_out, and_5_out, not_1_out, not_2_out, not_3_out, not_4_out,
       or_1_out;

  not not_1 (not_1_out, in_1[3]);
  not not_2 (not_2_out, in_1[1]);
  and and_1 (and_1_out, not_1_out, in_1[2]);
  not not_3 (not_3_out, in_1[0]);
  and and_2 (and_2_out, not_2_out, in_1[0]);
  and and_3 (and_3_out, and_1_out, not_3_out);
  and and_4 (and_4_out, in_1[3], in_1[1]);
  not not_4 (not_4_out, in_1[0]);
  or or_1 (or_1_out, and_2_out, and_3_out);
  and and_5 (and_5_out, and_4_out, not_4_out);
  or or_2 (yes_no, or_1_out, and_5_out);
endmodule
