// Logisim project MIPS_CPU.circ as structural Verilog: 10 circuits, main circuit main
module main (
  input  clr
);

  wire alu_1_zero, clk_out, control_1_alusel, control_1_dmwr, control_1_regwrite;
  wire [1:0] control_1_extop, control_1_lensel, control_1_npcop, control_1_wdsel, control_1_wrsel;
  wire [2:0] control_1_aluctrl;
  wire [4:0] multiplexer_1_out;
  wire [25:0] instrmemory_1_instr;
  wire [31:0] alu_1_aluout, datamemory_1_rd, ext_1_out_3, multiplexer_2_out, multiplexer_3_out, npc_1_npc,
       npc_1_pc_4, PC_q, regfile_1_rd1, regfile_1_rd2;
  wire [31:26] instrmemory_1_instr_2;

  Register #(.width(32)) PC (.D(npc_1_npc), .Q(PC_q), .clk(clk_out), .clr(clr));  // open: en
  Clock clk (.out(clk_out));
  InstrMemory instrmemory_1 (.PC(PC_q), .Instr({instrmemory_1_instr_2, instrmemory_1_instr}));
  NPC npc_1 (
    .PC(PC_q), .Imm26(instrmemory_1_instr), .RA(regfile_1_rd1), .PC_4(npc_1_pc_4), .NPC(npc_1_npc),
    .Zero(alu_1_zero), .NPCOp(control_1_npcop));
  Control control_1 (
    .Funct(instrmemory_1_instr[5:0]), .Opcode(instrmemory_1_instr_2), .NPCOp(control_1_npcop),
    .WRSel(control_1_wrsel), .WDSel(control_1_wdsel), .ExtOp(control_1_extop), .RegWrite(control_1_regwrite),
    .ALUSel(control_1_alusel), .ALUCtrl(control_1_aluctrl), .DMWr(control_1_dmwr), .LenSel(control_1_lensel));
  Multiplexer #(.select(2), .width(5)) multiplexer_1 (
    .in0(instrmemory_1_instr[20:16]), .in1(instrmemory_1_instr[15:11]), .in2({5{1'b1}}),
    .out(multiplexer_1_out), .sel(control_1_wrsel));  // open: in3, en
  Multiplexer #(.select(2), .width(32)) multiplexer_2 (
    .in0(alu_1_aluout), .in1(datamemory_1_rd), .in2(npc_1_pc_4), .out(multiplexer_2_out),
    .sel(control_1_wdsel));  // open: in3, en
  Ext ext_1 (.in_2(instrmemory_1_instr[15:0]), .out_3(ext_1_out_3), .ExtOp(control_1_extop));
  RegFile regfile_1 (
    .A1(instrmemory_1_instr[25:21]), .A2(instrmemory_1_instr[20:16]), .WE3(control_1_regwrite),
    .A3(multiplexer_1_out), .WD3(multiplexer_2_out), .RD1(regfile_1_rd1), .RD2(regfile_1_rd2), .clk(clk_out),
    .clr(clr));
  Multiplexer #(.width(32)) multiplexer_3 (
    .in0(regfile_1_rd2), .in1(ext_1_out_3), .out(multiplexer_3_out), .sel(control_1_alusel));  // open: en
  ALU alu_1 (
    .SrcB(regfile_1_rd1), .SrcA(multiplexer_3_out), .ALUOut(alu_1_aluout), .ALUCtrl(control_1_aluctrl),
    .Zero(alu_1_zero));
  DataMemory datamemory_1 (
    .LenSel(control_1_lensel), .A(alu_1_aluout), .WD(regfile_1_rd2), .RD(datamemory_1_rd),
    .DMWr(control_1_dmwr), .clk(clk_out), .clr(clr));

  // Notes on the sheet:
  //   NPCOp
  //   Reg_$ra
  //   WRSel
  //   WDSel
  //   ExtOp
  //   RegWrite
  //   ALUSel
  //   ALUCtrl
  //   DMWr
  //   LenSel
endmodule

module ALU (
  input  [2:0] ALUCtrl,
  input  [31:0] SrcB,
  input  [31:0] SrcA,
  output Zero,
  output [31:0] ALUOut
);

  wire [31:0] adder_1_out, and_1_out, multiplexer_1_out, not_1_out, or_1_out;

  assign not_1_out = ~SrcB;  // NOT_Gate not_1, 32 bits wide
  Multiplexer #(.width(32)) multiplexer_1 (
    .in0(SrcB), .in1(not_1_out), .out(multiplexer_1_out), .sel(ALUCtrl[2]));  // open: en
  Adder #(.width(32)) adder_1 (.a(multiplexer_1_out), .b(SrcA), .out(adder_1_out), .cin(ALUCtrl[2]));  // open: cout
  assign and_1_out = multiplexer_1_out & SrcA;  // AND_Gate and_1, 32 bits wide
  assign or_1_out = multiplexer_1_out | SrcA;  // OR_Gate or_1, 32 bits wide
  Multiplexer #(.select(2), .width(32)) multiplexer_2 (
    .in0(and_1_out), .in1(or_1_out), .in2(adder_1_out), .in3({{31{1'b0}}, adder_1_out[31]}), .out(ALUOut),
    .sel(ALUCtrl[1:0]));  // open: en
  Comparator #(.width(32), .mode("unsigned")) comparator_1 (.a({32{1'b0}}), .b(ALUOut), .eq(Zero));  // open: gt, lt
endmodule

module RegFile (
  input  [4:0] A1,
  input  [4:0] A2,
  input  WE3,
  input  [4:0] A3,
  input  [31:0] WD3,
  input  clk,
  input  clr,
  output [31:0] RD1,
  output [31:0] RD2
);

  wire demultiplexer_1_out0, demultiplexer_1_out1, demultiplexer_1_out2, demultiplexer_1_out3, WE_00000,
       WE_00001, WE_00010, WE_00011, WE_00100, WE_00101, WE_00110, WE_00111, WE_01000, WE_01001, WE_01010,
       WE_01011, WE_01100, WE_01101, WE_01110, WE_01111, WE_10000, WE_10001, WE_10010, WE_10011, WE_10100,
       WE_10101, WE_10110, WE_10111;
  wire [31:0] multiplexer_1_out, multiplexer_2_out, multiplexer_3_out, multiplexer_4_out, multiplexer_6_out,
       multiplexer_7_out, multiplexer_8_out, multiplexer_9_out, Read_00000, Read_00001, Read_00010,
       Read_00011, Read_00100, Read_00101, Read_00110, Read_00111, Read_01000, Read_01001, Read_01010,
       Read_01011, Read_01100, Read_01101, Read_01110, Read_01111, Read_10000, Read_10001, Read_10010,
       Read_10011, Read_10100, Read_10101, Read_10110, Read_10111, Read_11000, Read_11001, Read_11010,
       Read_11011, Read_11100, Read_11101, Read_11110, Read_11111;

  Demultiplexer #(.select(2)) demultiplexer_1 (
    .out0(demultiplexer_1_out0), .out1(demultiplexer_1_out1), .out2(demultiplexer_1_out2),
    .out3(demultiplexer_1_out3), .in(WE3), .sel(A3[4:3]));  // open: en
  Register #(.width(32)) register_1 (.D(WD3), .en(WE_00000), .Q(Read_00000), .clk(clk), .clr(clr));
  Register #(.width(32)) register_2 (.D(WD3), .en(WE_00001), .Q(Read_00001), .clk(clk), .clr(clr));
  Register #(.width(32)) register_3 (.D(WD3), .en(WE_00010), .Q(Read_00010), .clk(clk), .clr(clr));
  Register #(.width(32)) register_4 (.D(WD3), .en(WE_00011), .Q(Read_00011), .clk(clk), .clr(clr));
  Register #(.width(32)) register_5 (.D(WD3), .en(WE_00100), .Q(Read_00100), .clk(clk), .clr(clr));
  Register #(.width(32)) register_6 (.D(WD3), .en(WE_00101), .Q(Read_00101), .clk(clk), .clr(clr));
  Register #(.width(32)) register_7 (.D(WD3), .en(WE_00110), .Q(Read_00110), .clk(clk), .clr(clr));
  Register #(.width(32)) register_8 (.D(WD3), .en(WE_00111), .Q(Read_00111), .clk(clk), .clr(clr));
  Multiplexer #(.select(3), .width(32)) multiplexer_1 (
    .in0(Read_00000), .in1(Read_00001), .in2(Read_00010), .in3(Read_00011), .in4(Read_00100),
    .in5(Read_00101), .in6(Read_00110), .in7(Read_00111), .out(multiplexer_1_out), .sel(A1[2:0]));  // open: en
  Multiplexer #(.select(3), .width(32)) multiplexer_2 (
    .in0(Read_01000), .in1(Read_01001), .in2(Read_01010), .in3(Read_01011), .in4(Read_01100),
    .in5(Read_01101), .in6(Read_01110), .in7(Read_01111), .out(multiplexer_2_out), .sel(A1[2:0]));  // open: en
  Multiplexer #(.select(3), .width(32)) multiplexer_3 (
    .in0(Read_10000), .in1(Read_10001), .in2(Read_10010), .in3(Read_10011), .in4(Read_10100),
    .in5(Read_10101), .in6(Read_10110), .in7(Read_10111), .out(multiplexer_3_out), .sel(A1[2:0]));  // open: en
  Multiplexer #(.select(3), .width(32)) multiplexer_4 (
    .in0(Read_11000), .in1(Read_11001), .in2(Read_11010), .in3(Read_11011), .in4(Read_11100),
    .in5(Read_11101), .in6(Read_11110), .in7(Read_11111), .out(multiplexer_4_out), .sel(A1[2:0]));  // open: en
  Demultiplexer #(.select(3)) demultiplexer_2 (
    .out0(WE_00000), .out1(WE_00001), .out2(WE_00010), .out3(WE_00011), .out4(WE_00100), .out5(WE_00101),
    .out6(WE_00110), .out7(WE_00111), .in(demultiplexer_1_out0), .sel(A3[2:0]));  // open: en
  Demultiplexer #(.select(3)) demultiplexer_3 (
    .out0(WE_01000), .out1(WE_01001), .out2(WE_01010), .out3(WE_01011), .out4(WE_01100), .out5(WE_01101),
    .out6(WE_01110), .out7(WE_01111), .in(demultiplexer_1_out1), .sel(A3[2:0]));  // open: en
  Demultiplexer #(.select(3)) demultiplexer_4 (
    .out0(WE_10000), .out1(WE_10001), .out2(WE_10010), .out3(WE_10011), .out4(WE_10100), .out5(WE_10101),
    .out6(WE_10110), .out7(WE_10111), .in(demultiplexer_1_out2), .sel(A3[2:0]));  // open: en
  Demultiplexer #(.select(3)) demultiplexer_5 (
    .out0(WE_10000), .out1(WE_10001), .out2(WE_10010), .out3(WE_10011), .out4(WE_10100), .out5(WE_10101),
    .out6(WE_10110), .out7(WE_10111), .in(demultiplexer_1_out3), .sel(A3[2:0]));  // open: en
  Register #(.width(32)) register_9 (.D(WD3), .en(WE_01000), .Q(Read_01000), .clk(clk), .clr(clr));
  Register #(.width(32)) register_10 (.D(WD3), .en(WE_01001), .Q(Read_01001), .clk(clk), .clr(clr));
  Register #(.width(32)) register_11 (.D(WD3), .en(WE_01010), .Q(Read_01010), .clk(clk), .clr(clr));
  Register #(.width(32)) register_12 (.D(WD3), .en(WE_01011), .Q(Read_01011), .clk(clk), .clr(clr));
  Register #(.width(32)) register_13 (.D(WD3), .en(WE_01100), .Q(Read_01100), .clk(clk), .clr(clr));
  Register #(.width(32)) register_14 (.D(WD3), .en(WE_01101), .Q(Read_01101), .clk(clk), .clr(clr));
  Register #(.width(32)) register_15 (.D(WD3), .en(WE_01110), .Q(Read_01110), .clk(clk), .clr(clr));
  Register #(.width(32)) register_16 (.D(WD3), .en(WE_01111), .Q(Read_01111), .clk(clk), .clr(clr));
  Multiplexer #(.select(2), .width(32)) multiplexer_5 (
    .in0(multiplexer_1_out), .in1(multiplexer_2_out), .in2(multiplexer_3_out), .in3(multiplexer_4_out),
    .out(RD1), .sel(A1[4:3]));  // open: en
  Multiplexer #(.select(3), .width(32)) multiplexer_6 (
    .in0(Read_00000), .in1(Read_00001), .in2(Read_00010), .in3(Read_00011), .in4(Read_00100),
    .in5(Read_00101), .in6(Read_00110), .in7(Read_00111), .out(multiplexer_6_out), .sel(A2[2:0]));  // open: en
  Multiplexer #(.select(3), .width(32)) multiplexer_7 (
    .in0(Read_01000), .in1(Read_01001), .in2(Read_01010), .in3(Read_01011), .in4(Read_01100),
    .in5(Read_01101), .in6(Read_01110), .in7(Read_01111), .out(multiplexer_7_out), .sel(A2[2:0]));  // open: en
  Multiplexer #(.select(3), .width(32)) multiplexer_8 (
    .in0(Read_10000), .in1(Read_10001), .in2(Read_10010), .in3(Read_10011), .in4(Read_10100),
    .in5(Read_10101), .in6(Read_10110), .in7(Read_10111), .out(multiplexer_8_out), .sel(A2[2:0]));  // open: en
  Multiplexer #(.select(3), .width(32)) multiplexer_9 (
    .in0(Read_11000), .in1(Read_11001), .in2(Read_11010), .in3(Read_11011), .in4(Read_11100),
    .in5(Read_11101), .in6(Read_11110), .in7(Read_11111), .out(multiplexer_9_out), .sel(A2[2:0]));  // open: en
  Register #(.width(32)) register_17 (.D(WD3), .en(WE_10000), .Q(Read_10000), .clk(clk), .clr(clr));
  Register #(.width(32)) register_18 (.D(WD3), .en(WE_10001), .Q(Read_10001), .clk(clk), .clr(clr));
  Register #(.width(32)) register_19 (.D(WD3), .en(WE_10010), .Q(Read_10010), .clk(clk), .clr(clr));
  Register #(.width(32)) register_20 (.D(WD3), .en(WE_10011), .Q(Read_10011), .clk(clk), .clr(clr));
  Register #(.width(32)) register_21 (.D(WD3), .en(WE_10100), .Q(Read_10100), .clk(clk), .clr(clr));
  Register #(.width(32)) register_22 (.D(WD3), .en(WE_10101), .Q(Read_10101), .clk(clk), .clr(clr));
  Register #(.width(32)) register_23 (.D(WD3), .en(WE_10110), .Q(Read_10110), .clk(clk), .clr(clr));
  Register #(.width(32)) register_24 (.D(WD3), .en(WE_10111), .Q(Read_10111), .clk(clk), .clr(clr));
  Multiplexer #(.select(2), .width(32)) multiplexer_10 (
    .in0(multiplexer_6_out), .in1(multiplexer_7_out), .in2(multiplexer_8_out), .in3(multiplexer_9_out),
    .out(RD2), .sel(A2[4:3]));  // open: en
  Register #(.width(32)) register_25 (.D(WD3), .en(WE_10000), .Q(Read_11000), .clk(clk), .clr(clr));
  Register #(.width(32)) register_26 (.D(WD3), .en(WE_10001), .Q(Read_11001), .clk(clk), .clr(clr));
  Register #(.width(32)) register_27 (.D(WD3), .en(WE_10010), .Q(Read_11010), .clk(clk), .clr(clr));
  Register #(.width(32)) register_28 (.D(WD3), .en(WE_10011), .Q(Read_11011), .clk(clk), .clr(clr));
  Register #(.width(32)) register_29 (.D(WD3), .en(WE_10100), .Q(Read_11100), .clk(clk), .clr(clr));
  Register #(.width(32)) register_30 (.D(WD3), .en(WE_10101), .Q(Read_11101), .clk(clk), .clr(clr));
  Register #(.width(32)) register_31 (.D(WD3), .en(WE_10110), .Q(Read_11110), .clk(clk), .clr(clr));
  Register #(.width(32)) register_32 (.D(WD3), .en(WE_10111), .Q(Read_11111), .clk(clk), .clr(clr));
endmodule

module signedExt (
  input  [15:0] in_1,
  output [31:0] out_2
);


  assign out_2 = {{17{in_1[15]}}, in_1[14:0]};
endmodule

module Control (
  input  [5:0] Funct,
  input  [5:0] Opcode,
  output [1:0] NPCOp,
  output [1:0] WRSel,
  output [1:0] WDSel,
  output [1:0] ExtOp,
  output RegWrite,
  output ALUSel,
  output [2:0] ALUCtrl,
  output DMWr,
  output [1:0] LenSel
);

  wire and_1_out, and_2_out, and_3_out, and_4_out, not_1_out, not_2_out, not_3_out, not_4_out, not_5_out,
       not_6_out, not_7_out, not_8_out, not_9_out, not_10_out, not_11_out, not_12_out;

  not not_1 (not_1_out, Opcode[1]);
  not not_2 (not_2_out, Opcode[0]);
  not not_3 (not_3_out, Opcode[2]);
  not not_4 (not_4_out, Opcode[3]);
  not not_5 (not_5_out, Opcode[4]);
  not not_6 (not_6_out, Opcode[5]);
  and and_1 (and_1_out, not_2_out, not_1_out, not_3_out, not_4_out, not_5_out, not_6_out);
  and and_2 (and_2_out, not_2_out, not_1_out, not_3_out, Opcode[3], not_5_out, not_6_out);
  not not_7 (not_7_out, Funct[1]);
  not not_8 (not_8_out, Funct[0]);
  not not_9 (not_9_out, Funct[2]);
  not not_10 (not_10_out, Funct[3]);
  not not_11 (not_11_out, Funct[4]);
  not not_12 (not_12_out, Funct[5]);
  and and_3 (and_3_out, not_8_out, not_7_out, not_9_out, not_10_out, not_11_out, Funct[5]);
  and and_4 (and_4_out, and_3_out, and_1_out);
  buf or_1 (NPCOp[1], 1'b0);  // OR_Gate
  buf or_2 (NPCOp[0], 1'b0);  // OR_Gate
  buf or_3 (WRSel[1], 1'b0);  // OR_Gate
  or or_4 (WRSel[0], 1'b0, and_4_out);
  buf or_5 (WDSel[1], 1'b0);  // OR_Gate
  buf or_6 (WDSel[0], 1'b0);  // OR_Gate
  buf or_7 (ExtOp[1], 1'b0);  // OR_Gate
  buf or_8 (ExtOp[0], 1'b0);  // OR_Gate
  or or_9 (RegWrite, 1'b0, and_4_out, and_2_out);
  or or_10 (ALUSel, 1'b0, and_2_out);
  buf or_11 (ALUCtrl[2], 1'b0);  // OR_Gate
  or or_12 (ALUCtrl[1], 1'b0, and_4_out, and_2_out);
  buf or_13 (ALUCtrl[0], 1'b0);  // OR_Gate
  buf or_14 (DMWr, 1'b0);  // OR_Gate
  buf or_15 (LenSel[1], 1'b0);  // OR_Gate
  buf or_16 (LenSel[0], 1'b0);  // OR_Gate

  // Notes on the sheet:
  //   special(R)
  //   add
  //   addi
endmodule

module NPC (
  input  [31:0] PC,
  input  [25:0] Imm26,
  input  [31:0] RA,
  input  Zero,
  input  [1:0] NPCOp,
  output [31:0] PC_4,
  output [31:0] NPC
);

  wire [31:0] adder_2_out, multiplexer_1_out;

  Adder #(.width(32)) adder_1 (.a(32'h4), .b(PC), .out(PC_4));  // open: cin, cout
  Adder #(.width(32)) adder_2 (
    .a(PC_4), .b({{5{Imm26[25]}}, Imm26[24:0], 2'b00}), .out(adder_2_out));  // open: cin, cout
  Multiplexer #(.width(32)) multiplexer_1 (
    .in0(PC_4), .in1(adder_2_out), .out(multiplexer_1_out), .sel(Zero));  // open: en
  Multiplexer #(.select(2), .width(32)) multiplexer_2 (
    .in0(PC_4), .in1(multiplexer_1_out), .in2({PC[31:28], Imm26, 2'b00}), .in3(RA), .out(NPC), .sel(NPCOp));  // open: en
endmodule

module unsignedExt (
  input  [15:0] in_1,
  output [31:0] out_2
);


  assign out_2 = {{16{1'b0}}, in_1};
endmodule

module Ext (
  input  [1:0] ExtOp,
  input  [15:0] in_2,
  output [31:0] out_3
);

  wire [31:0] signedext_1_out_2, unsignedext_1_out_2;

  signedExt signedext_1 (.in_1(in_2), .out_2(signedext_1_out_2));
  unsignedExt unsignedext_1 (.in_1(in_2), .out_2(unsignedext_1_out_2));
  Multiplexer #(.select(2), .width(32)) multiplexer_1 (
    .in0(signedext_1_out_2), .in1(unsignedext_1_out_2), .in2({in_2, {16{1'b0}}}), .out(out_3), .sel(ExtOp));  // open: in3, en
endmodule

module InstrMemory (
  input  [31:0] PC,
  output [31:0] Instr
);

  ROM #(.addrWidth(5), .dataWidth(32)) rom_1 (.addr(PC[6:2]), .data(Instr));  // open: sel

  // Notes on the sheet:
  //   contents of rom_1 (hex, n*v repeats v):
  //   21290005 214a0004 12a5820
endmodule

module DataMemory (
  input  [1:0] LenSel,
  input  [31:0] A,
  input  DMWr,
  input  clk,
  input  clr,
  input  [31:0] WD,
  output [31:0] RD
);

  wire decoder_1_out0, decoder_1_out1, decoder_1_out2, decoder_1_out3, decoder_2_out0, decoder_2_out1;
  wire [7:0] _0_7, _8_15, _16_23, _24_31, multiplexer_6_out, multiplexer_8_out;
  wire [15:0] multiplexer_3_out, multiplexer_5_out, multiplexer_9_out;
  wire [23:0] multiplexer_1_out;
  wire [31:0] multiplexer_7_out;

  Decoder #(.select(2)) decoder_1 (
    .out0(decoder_1_out0), .out1(decoder_1_out1), .out2(decoder_1_out2), .out3(decoder_1_out3), .sel(A[1:0]));  // open: en
  Decoder decoder_2 (.out0(decoder_2_out0), .out1(decoder_2_out1), .sel(A[1]));  // open: en
  Multiplexer #(.width(8)) multiplexer_1 (
    .in0(WD[7:0]), .in1(_0_7), .out(multiplexer_1_out[7:0]), .sel(decoder_1_out0));  // open: en
  Multiplexer #(.width(8)) multiplexer_2 (
    .in0(WD[7:0]), .in1(_8_15), .out(multiplexer_1_out[15:8]), .sel(decoder_1_out1));  // open: en
  Multiplexer #(.width(16)) multiplexer_3 (
    .in0(WD[15:0]), .in1({_8_15, _0_7}), .out(multiplexer_3_out), .sel(decoder_2_out0));  // open: en
  Multiplexer #(.width(8)) multiplexer_4 (
    .in0(WD[7:0]), .in1(_16_23), .out(multiplexer_1_out[23:16]), .sel(decoder_1_out2));  // open: en
  Multiplexer #(.width(16)) multiplexer_5 (
    .in0(WD[15:0]), .in1({_24_31, _16_23}), .out(multiplexer_5_out), .sel(decoder_2_out1));  // open: en
  Multiplexer #(.width(8)) multiplexer_6 (
    .in0(WD[7:0]), .in1(_24_31), .out(multiplexer_6_out), .sel(decoder_1_out3));  // open: en
  Multiplexer #(.select(2), .width(32)) multiplexer_7 (
    .in0(WD), .in1({multiplexer_6_out, multiplexer_1_out}), .in2({multiplexer_5_out, multiplexer_3_out}),
    .out(multiplexer_7_out), .sel(LenSel));  // open: in3, en
  RAM #(.addrWidth(5), .dataWidth(32), .bus("separate")) ram_1 (
    .addr(A[6:2]), .din(multiplexer_7_out), .data({_24_31, _16_23, _8_15, _0_7}), .str(DMWr), .clk(clk),
    .clr(clr));  // open: sel, ld
  Multiplexer #(.select(2), .width(8)) multiplexer_8 (
    .in0(_0_7), .in1(_8_15), .in2(_16_23), .in3(_24_31), .out(multiplexer_8_out), .sel(A[1:0]));  // open: en
  Multiplexer #(.width(16)) multiplexer_9 (
    .in0({_8_15, _0_7}), .in1({_24_31, _16_23}), .out(multiplexer_9_out), .sel(A[1]));  // open: en
  Multiplexer #(.select(2), .width(32)) multiplexer_10 (
    .in0({_24_31, _16_23, _8_15, _0_7}), .in1({{24{1'b0}}, multiplexer_8_out}),
    .in2({{16{1'b0}}, multiplexer_9_out}), .out(RD), .sel(LenSel));  // open: in3, en
endmodule
